// Logisim project Processor.circ as structural Verilog: 42 circuits, main circuit main
module main (
);

  wire not_1_out, processor_1_output_available;
  wire [23:0] counter_1_q;
  wire [31:0] processor_1_out_1;

  Processor processor_1 (.out_1(processor_1_out_1), .Output_Available(processor_1_output_available));
  not not_1 (not_1_out, processor_1_output_available);
  Counter #(.width(24), .max('hffffff)) counter_1 (
    .count(1'b1), .Q(counter_1_q), .clk(not_1_out));  // open: load, D, carry, clr
  RAM #(.addrWidth(24), .dataWidth(32), .bus("separate")) ram_1 (
    .addr(counter_1_q), .din(processor_1_out_1), .str(1'b1), .sel(1'b1), .clk(not_1_out), .ld(1'b1));  // open: data, clr
endmodule

module Processor (
  output [31:0] out_1,
  output Output_Available
);

  wire ALU_Arith_Logic, ALU_CMP, ALU_I0_Reg_Enable, ALU_Pass_Through_I0, and_1_out, clock_1_out, clock_2_out,
       clock_3_out, Cond_JMP, Cond_JMP_Enable, Cond_JMP_Reg_Enable, control_unit_1_state_input, Enable_JMP,
       IP_plus_plus, IR_Load, JMP_Reg_Enable, not_1_out, not_2_out, or_1_out, RAM_Addr_Reg_Enable,
       RAM_Addr_Reg_Pass_Through, RAM_Addr_Reg_Temp_Enable, RAM_Addr_Reg_Temp_Use, RAM_Data_Reg_Pass_through,
       RAM_Write_Data;
  wire [1:0] ALU_I1_Reg_Sel, RAM_Data_Reg_Sel;
  wire [2:0] ALU_Mode, Cond_JMP_Mode, cu_fsm_1_state;
  wire [23:0] counter_1_q, multiplexer_1_out, n24_bit_register_1_q, n24_bit_register_2_q,
       n24_bit_register_3_q;
  wire [31:0] ALU, IR_q, n32_bit_register_1_q, n32_bit_register_2_q, n32_bit_register_mux_with_1_q,
       n32_bit_register_mux_with_2_q, RAM, ROM;

  or or_1 (or_1_out, Cond_JMP, Enable_JMP);
  not not_1 (not_1_out, or_1_out);
  and and_1 (and_1_out, not_1_out, IP_plus_plus);
  // Probe on RAM_Data_Reg_Sel
  CU_FSM cu_fsm_1 (.Input(control_unit_1_state_input), .State(cu_fsm_1_state));
  Register #(.width(32)) IR (.D(ROM), .en(IR_Load), .Q(IR_q), .clk(clock_1_out));  // open: clr
  Clock clock_1 (.out(clock_1_out));
  _24_Bit_Register u_24_bit_register_1 (
    .Input(ROM[23:0]), .Enable(JMP_Reg_Enable), .Pass_through(1'b0), .Q(n24_bit_register_1_q));
  Counter #(.width(24), .max('hffffff)) counter_1 (
    .load(or_1_out), .D(n24_bit_register_1_q), .count(and_1_out), .Q(counter_1_q), .clk(clock_2_out));  // open: carry, clr
  Clock clock_2 (.out(clock_2_out));
  _24_Bit_Register u_24_bit_register_2 (
    .Input(ROM[23:0]), .Enable(RAM_Addr_Reg_Temp_Enable), .Pass_through(1'b0), .Q(n24_bit_register_2_q));
  _24_Bit_Register u_24_bit_register_3 (
    .Input(ROM[23:0]), .Enable(RAM_Addr_Reg_Enable), .Pass_through(RAM_Addr_Reg_Pass_Through),
    .Q(n24_bit_register_3_q));
  not not_2 (not_2_out, RAM_Addr_Reg_Temp_Use);
  _32_Bit_Register_MUX_with u_32_bit_register_mux_with_1 (
    .I1(ROM), .I2(ALU), .I3(RAM), .Sel(RAM_Data_Reg_Sel), .Q(n32_bit_register_mux_with_1_q),
    .Pass_through(RAM_Data_Reg_Pass_through));
  // Probe on cu_fsm_1_state
  Multiplexer #(.width(24)) multiplexer_1 (
    .in0(n24_bit_register_2_q), .in1(n24_bit_register_3_q), .out(multiplexer_1_out), .sel(not_2_out));  // open: en
  ROM #(.addrWidth(24), .dataWidth(32)) rom_1 (.addr(counter_1_q), .data(ROM), .sel(1'b1));
  RAM #(.addrWidth(24), .dataWidth(32), .bus("separate")) ram_1 (
    .addr(multiplexer_1_out), .din(n32_bit_register_mux_with_1_q), .data(RAM), .str(RAM_Write_Data),
    .sel(1'b1), .clk(clock_3_out), .ld(1'b1));  // open: clr
  Clock clock_3 (.out(clock_3_out));
  Control_Unit control_unit_1 (
    .State(cu_fsm_1_state), .Instruction(IR_q[4:0]), .State_Input(control_unit_1_state_input),
    .IP_plus_plus(IP_plus_plus), .IR_Load(IR_Load), .RAM_Addr_Reg_Enable(RAM_Addr_Reg_Enable),
    .RAM_Data_Reg_Sel(RAM_Data_Reg_Sel), .RAM_Write_Data(RAM_Write_Data), .ALU_I1_Reg_Sel(ALU_I1_Reg_Sel),
    .ALU_I0_Reg_Enable(ALU_I0_Reg_Enable), .ALU_Arith_Logic(ALU_Arith_Logic),
    .Cond_JMP_Enable(Cond_JMP_Enable), .ALU_Mode(ALU_Mode), .Cond_JMP_Mode(Cond_JMP_Mode), .ALU_CMP(ALU_CMP),
    .RAM_Data_Reg_Pass_through(RAM_Data_Reg_Pass_through), .ALU_Pass_Through_I0(ALU_Pass_Through_I0),
    .Enable_JMP(Enable_JMP), .JMP_Reg_Enable(JMP_Reg_Enable),
    .RAM_Addr_Reg_Pass_through(RAM_Addr_Reg_Pass_Through), .Cond_JMP_Reg_Enable(Cond_JMP_Reg_Enable),
    .Output_Reg_Enable(Output_Available), .RAM_Addr_Reg_Temp_Enable(RAM_Addr_Reg_Temp_Enable),
    .RAM_Addr_Reg_Temp_Use(RAM_Addr_Reg_Temp_Use));
  // Probe on ALU_I1_Reg_Sel
  _32_Bit_Register_MUX_with u_32_bit_register_mux_with_2 (
    .I1(ROM), .I2(RAM), .Sel(ALU_I1_Reg_Sel), .Q(n32_bit_register_mux_with_2_q), .Pass_through(1'b0));  // open: I3
  _32_Bit_Register u_32_bit_register_1 (
    .Input(RAM), .Enable(ALU_I0_Reg_Enable), .Pass_through(1'b0), .Q(n32_bit_register_1_q));
  // Probe on n32_bit_register_1_q
  // Probe on n32_bit_register_mux_with_2_q
  _32_Bit_Register u_32_bit_register_2 (
    .Input(ALU), .Enable(Cond_JMP_Reg_Enable), .Pass_through(1'b0), .Q(n32_bit_register_2_q));
  // Probe on n32_bit_register_2_q[2:0]
  ALU alu_1 (
    .I0(n32_bit_register_1_q), .I1(n32_bit_register_mux_with_2_q), .Cin(1'b0),
    .Pass_Through_I0(ALU_Pass_Through_I0), .Arith_Logic(ALU_Arith_Logic), .CMP(ALU_CMP), .out_8(ALU),
    .Mode(ALU_Mode));  // open: Cout
  // Probe on ALU
  Conditional_JMP_CMP_Unit conditional_jmp_cmp_unit_1 (
    .Enable(Cond_JMP_Enable), .I0(n32_bit_register_2_q[2:0]), .Mode(Cond_JMP_Mode), .Q(Cond_JMP),
    .I1(n32_bit_register_2_q));
  _32_Bit_Register u_32_bit_register_3 (.Input(RAM), .Enable(Output_Available), .Pass_through(1'b0), .Q(out_1));

  // Other names for the same wires on the sheet: Output_Reg_Enable = Output_Available

  // Notes on the sheet:
  //   ROM
  //   Temp
  //   Main
  //   State
  //   CU
  //   contents of rom_1 (hex, n*v repeats v):
  //   d 0 5 d 1 0 d 2 1 d 3 1 1b 1 1b 2 6 3 1 c 1 2 c 2 3 1b 3 18 0 16 10
  //   RAM
  //   ALU
  //   Cond JMP CMP
  //   Output
endmodule

module _24_Bit_Register (
  input  [23:0] Input,
  input  Enable,
  input  Pass_through,
  output [23:0] Q
);

  wire clock_1_out, not_1_out, or_1_out;
  wire [23:0] register_1_q;

  or or_1 (or_1_out, Enable, Pass_through);
  Clock clock_1 (.out(clock_1_out));
  Multiplexer #(.width(24)) multiplexer_1 (.in0(Input), .in1(register_1_q), .out(Q), .sel(not_1_out));  // open: en
  Register #(.width(24)) register_1 (.D(Input), .en(or_1_out), .Q(register_1_q), .clk(clock_1_out));  // open: clr
  not not_1 (not_1_out, Pass_through);
endmodule

module _32_Bit_Register (
  input  [31:0] Input,
  input  Enable,
  input  Pass_through,
  output [31:0] Q
);

  wire clock_1_out, not_1_out, or_1_out;
  wire [31:0] register_1_q;

  or or_1 (or_1_out, Enable, Pass_through);
  Clock clock_1 (.out(clock_1_out));
  Multiplexer #(.width(32)) multiplexer_1 (.in0(Input), .in1(register_1_q), .out(Q), .sel(not_1_out));  // open: en
  Register #(.width(32)) register_1 (.D(Input), .en(or_1_out), .Q(register_1_q), .clk(clock_1_out));  // open: clr
  not not_1 (not_1_out, Pass_through);
endmodule

module _32_Bit_Register_MUX_with (
  input  [31:0] I1,
  input  [31:0] I2,
  input  [31:0] I3,
  input  [1:0] Sel,
  input  Pass_through,
  output [31:0] Q
);

  wire clock_1_out, not_1_out, or_1_out;
  wire [31:0] multiplexer_1_out, register_1_q;

  Multiplexer #(.select(2), .width(32)) multiplexer_1 (
    .in1(I1), .in2(I2), .in3(I3), .out(multiplexer_1_out), .sel(Sel));  // open: in0, en
  or or_1 (or_1_out, Sel[0], Sel[1]);
  Clock clock_1 (.out(clock_1_out));
  Register #(.width(32)) register_1 (
    .D(multiplexer_1_out), .en(or_1_out), .Q(register_1_q), .clk(clock_1_out));  // open: clr
  not not_1 (not_1_out, Pass_through);
  Multiplexer #(.width(32)) multiplexer_2 (
    .in0(multiplexer_1_out), .in1(register_1_q), .out(Q), .sel(not_1_out));  // open: en
endmodule

module ALU (
  input  [31:0] I0,
  input  [31:0] I1,
  input  Cin,
  input  [2:0] Mode,
  input  Pass_Through_I0,
  input  Arith_Logic,
  input  CMP,
  output [31:0] out_8,
  output Cout
);

  wire [1:0] alu_output_mux_select_1_out_4;
  wire [31:0] alu_cmp_unit_1_out_3, alu_logic_unit_1_q, arithmetic_unit_1_q;

  Arithmetic_Unit arithmetic_unit_1 (.I0(I0), .I1(I1), .Mode(Mode), .Q(arithmetic_unit_1_q), .Cin(Cin), .Cout(Cout));
  ALU_Logic_Unit alu_logic_unit_1 (.I0(I0), .I1(I1), .Mode(Mode), .Q(alu_logic_unit_1_q));
  ALU_CMP_Unit alu_cmp_unit_1 (.I0(I0), .I1(I1), .out_3(alu_cmp_unit_1_out_3));
  // Probe on alu_output_mux_select_1_out_4
  ALU_Output_MUX_Select alu_output_mux_select_1 (
    .Pass_Through_A(Pass_Through_I0), .Arith_Logic(Arith_Logic), .CMP(CMP),
    .out_4(alu_output_mux_select_1_out_4));
  Multiplexer #(.select(2), .width(32)) multiplexer_1 (
    .in0(I0), .in1(arithmetic_unit_1_q), .in2(alu_logic_unit_1_q), .in3(alu_cmp_unit_1_out_3), .out(out_8),
    .sel(alu_output_mux_select_1_out_4));  // open: en
endmodule

module ALU_Output_MUX_Select (
  input  Pass_Through_A,
  input  Arith_Logic,
  input  CMP,
  output [1:0] out_4
);

  wire and_1_out, and_2_out, and_3_out, and_4_out, not_1_out, not_2_out;

  not not_1 (not_1_out, Pass_Through_A);
  not not_2 (not_2_out, Arith_Logic);
  and and_1 (and_1_out, Arith_Logic, not_1_out);
  and and_2 (and_2_out, CMP, not_1_out);
  and and_3 (and_3_out, not_2_out, not_1_out);
  and and_4 (and_4_out, CMP, not_1_out);
  or or_1 (out_4[0], and_1_out, and_2_out);
  or or_2 (out_4[1], and_3_out, and_4_out);
endmodule

module Arithmetic_Unit (
  input  Cin,
  input  [31:0] I0,
  input  [31:0] I1,
  input  [2:0] Mode,
  output [31:0] Q,
  output Cout
);

  wire adder_1_cout, arithmetic_unit_mux_select_1_mux_add, arithmetic_unit_mux_select_1_mux_sub,
       subtractor_1_bout;
  wire [1:0] arithmetic_unit_mux_select_1_mux_output;
  wire [31:0] adder_1_out, multiplexer_1_out, multiplexer_2_out, subtractor_1_out;

  Multiplexer #(.width(32)) multiplexer_1 (
    .in0(I1), .in1(32'h1), .out(multiplexer_1_out), .sel(arithmetic_unit_mux_select_1_mux_add));  // open: en
  Arithmetic_Unit_MUX_Select arithmetic_unit_mux_select_1 (
    .S0(Mode[0]), .S1(Mode[1]), .S2(Mode[2]), .MUX_Add(arithmetic_unit_mux_select_1_mux_add),
    .Mux_Sub(arithmetic_unit_mux_select_1_mux_sub), .MUX_Output(arithmetic_unit_mux_select_1_mux_output));
  Adder #(.width(32)) adder_1 (.a(I0), .b(multiplexer_1_out), .out(adder_1_out), .cin(Cin), .cout(adder_1_cout));
  Multiplexer #(.width(32)) multiplexer_2 (
    .in0(I1), .in1(32'h1), .out(multiplexer_2_out), .sel(arithmetic_unit_mux_select_1_mux_sub));  // open: en
  Subtractor #(.width(32)) subtractor_1 (
    .a(I0), .b(multiplexer_2_out), .out(subtractor_1_out), .bin(Cin), .bout(subtractor_1_bout));
  Multiplexer #(.select(2), .width(32)) multiplexer_3 (
    .in0(adder_1_out), .in1(subtractor_1_out), .out(Q), .sel(arithmetic_unit_mux_select_1_mux_output));  // open: in2, in3, en
  // Probe on arithmetic_unit_mux_select_1_mux_output
  Multiplexer #(.select(2)) multiplexer_4 (
    .in0(adder_1_cout), .in1(subtractor_1_bout), .out(Cout), .sel(arithmetic_unit_mux_select_1_mux_output));  // open: in2, in3, en
endmodule

module Arithmetic_Unit_MUX_Select (
  input  S0,
  input  S1,
  input  S2,
  output MUX_Add,
  output Mux_Sub,
  output [1:0] MUX_Output
);

  wire not_1_out, not_2_out, not_3_out;

  not not_1 (not_1_out, S2);
  not not_2 (not_2_out, S1);
  not not_3 (not_3_out, S0);
  and and_1 (MUX_Add, S1, not_3_out, not_1_out);
  and and_2 (Mux_Sub, S0, S1, not_1_out);
  and and_3 (MUX_Output[0], S0, not_1_out);
  and and_4 (MUX_Output[1], not_1_out, S2);
endmodule

module ALU_Logic_Unit (
  input  [31:0] I0,
  input  [31:0] I1,
  input  [2:0] Mode,
  output [31:0] Q
);

  wire [31:0] and_1_out, not_1_out, or_1_out, xor_1_out;

  assign not_1_out = ~I0;  // NOT_Gate not_1, 32 bits wide
  assign or_1_out = I0 | I1;  // OR_Gate or_1, 32 bits wide
  assign and_1_out = I0 & I1;  // AND_Gate and_1, 32 bits wide
  assign xor_1_out = I0 ^ I1;  // XOR_Gate xor_1, 32 bits wide
  Multiplexer #(.select(2), .width(32)) multiplexer_1 (
    .in0(not_1_out), .in1(or_1_out), .in2(and_1_out), .in3(xor_1_out), .out(Q), .sel(Mode[1:0]));  // open: en
  // Probe on Mode[1:0]
endmodule

module ALU_CMP_Unit (
  input  [31:0] I0,
  input  [31:0] I1,
  output [31:0] out_3
);

  Comparator #(.width(32)) comparator_1 (.a(I0), .b(I1), .gt(out_3[0]), .eq(out_3[1]), .lt(out_3[2]));

  assign out_3[31:3] = {29{1'b0}};
endmodule

module Conditional_JMP_CMP_Unit (
  input  [2:0] Mode,
  input  [2:0] I0,
  input  Enable,
  input  [31:0] I1,
  output Q
);

  wire and_7_out, and_8_out, and_9_out, and_10_out, comparator_1_eq, comparator_2_eq, not_1_out, not_2_out,
       not_3_out, not_4_out, or_1_out, or_3_out, or_4_out, xor_1_out, xor_2_out;
  wire [0:0] and_3_out, and_6_out;
  wire [1:1] and_1_out, and_2_out;
  wire [2:0] or_2_out;
  wire [2:2] and_4_out, and_5_out;

  not not_1 (not_1_out, Mode[2]);
  not not_2 (not_2_out, Mode[1]);
  not not_3 (not_3_out, Mode[0]);
  and and_1 (and_1_out[1], not_3_out, not_2_out, not_1_out);
  and and_2 (and_2_out[1], Mode[0], not_2_out, not_1_out);
  and and_3 (and_3_out[0], not_3_out, Mode[1], not_1_out);
  and and_4 (and_4_out[2], Mode[0], Mode[1], not_1_out);
  and and_5 (and_5_out[2], not_3_out, not_2_out, Mode[2]);
  and and_6 (and_6_out[0], Mode[0], not_2_out, Mode[2]);
  and and_7 (and_7_out, not_3_out, Mode[1], Mode[2]);
  and and_8 (and_8_out, Mode[0], Mode[1], Mode[2]);
  or or_1 (or_1_out, and_7_out, and_8_out);
  assign or_2_out = {1'b0, and_1_out[1], 1'b0} | {1'b0, and_2_out[1], 1'b0} | {2'b00, and_3_out[0]} | {and_4_out[2], 2'b00} | {and_5_out[2], 2'b00} | {2'b00, and_6_out[0]};  // OR_Gate or_2, 3 bits wide
  Comparator #(.width(32), .mode("unsigned")) comparator_1 (
    .a(I1), .b({32{1'b0}}), .eq(comparator_1_eq));  // open: gt, lt
  or or_3 (or_3_out, and_6_out[0], and_4_out[2], and_2_out[1]);
  Comparator #(.width(3), .mode("unsigned")) comparator_2 (.a(I0), .b(or_2_out), .eq(comparator_2_eq));  // open: gt, lt
  not not_4 (not_4_out, or_1_out);
  xor xor_1 (xor_1_out, and_8_out, comparator_1_eq);
  xor xor_2 (xor_2_out, or_3_out, comparator_2_eq);
  and and_9 (and_9_out, xor_2_out, not_4_out);
  and and_10 (and_10_out, or_1_out, xor_1_out);
  or or_4 (or_4_out, and_9_out, and_10_out);
  and and_11 (Q, Enable, or_4_out);

  // Notes on the sheet:
  //   0 - je
  //   1 - jne
  //   2 - jg
  //   3 - jge
  //   4 - jl
  //   5 - jle
  //   6 - jz
  //   7 - jnz
  //   This analyzes the last 3 bits - output of CMP
  //   This analyzes all 32 bits
  //   Invert
endmodule

module Control_Unit (
  input  [2:0] State,
  input  [4:0] Instruction,
  output IR_Load,
  output IP_plus_plus,
  output State_Input,
  output Cond_JMP_Reg_Enable,
  output RAM_Addr_Reg_Enable,
  output RAM_Addr_Reg_Pass_through,
  output [1:0] RAM_Data_Reg_Sel,
  output RAM_Data_Reg_Pass_through,
  output RAM_Write_Data,
  output RAM_Addr_Reg_Temp_Enable,
  output RAM_Addr_Reg_Temp_Use,
  output ALU_I0_Reg_Enable,
  output [1:0] ALU_I1_Reg_Sel,
  output ALU_CMP,
  output ALU_Arith_Logic,
  output ALU_Pass_Through_I0,
  output [2:0] ALU_Mode,
  output Cond_JMP_Enable,
  output Enable_JMP,
  output [2:0] Cond_JMP_Mode,
  output JMP_Reg_Enable,
  output Output_Reg_Enable
);

  wire ALU_Arith_Logic_6, ALU_Arith_Logic_7, ALU_Arith_Logic_8, ALU_Arith_Logic_9, ALU_Arith_Logic_23,
       ALU_Arith_Logic_24, ALU_CMP_10, ALU_CMP_11, ALU_I0_Reg_Enable_0, ALU_I0_Reg_Enable_1,
       ALU_I0_Reg_Enable_2, ALU_I0_Reg_Enable_3, ALU_I0_Reg_Enable_4, ALU_I0_Reg_Enable_5,
       ALU_I0_Reg_Enable_6, ALU_I0_Reg_Enable_7, ALU_I0_Reg_Enable_8, ALU_I0_Reg_Enable_9,
       ALU_I0_Reg_Enable_10, ALU_I0_Reg_Enable_11, ALU_I0_Reg_Enable_23, ALU_I0_Reg_Enable_24,
       ALU_I0_Reg_Enable_25, ALU_I0_Reg_Enable_26, and_2_out, and_3_out, Cond_JMP_Enable_15,
       Cond_JMP_Enable_16, Cond_JMP_Enable_17, Cond_JMP_Enable_18, Cond_JMP_Enable_19, Cond_JMP_Enable_20,
       Cond_JMP_Enable_21, Cond_JMP_Enable_22, JMP_Reg_Enable_14, JMP_Reg_Enable_15, JMP_Reg_Enable_16,
       JMP_Reg_Enable_17, JMP_Reg_Enable_18, JMP_Reg_Enable_19, JMP_Reg_Enable_20, JMP_Reg_Enable_21,
       JMP_Reg_Enable_22, not_1_out, not_2_out, not_3_out, RAM_Addr_Reg_Pass_through_0,
       RAM_Addr_Reg_Pass_through_1, RAM_Addr_Reg_Pass_through_2, RAM_Addr_Reg_Pass_through_3,
       RAM_Addr_Reg_Pass_through_4, RAM_Addr_Reg_Pass_through_5, RAM_Addr_Reg_Pass_through_6,
       RAM_Addr_Reg_Pass_through_7, RAM_Addr_Reg_Pass_through_8, RAM_Addr_Reg_Pass_through_9,
       RAM_Addr_Reg_Pass_through_10, RAM_Addr_Reg_Pass_through_11, RAM_Addr_Reg_Pass_through_12,
       RAM_Addr_Reg_Pass_through_23, RAM_Addr_Reg_Pass_through_24, RAM_Addr_Reg_Pass_through_25,
       RAM_Addr_Reg_Pass_through_26, RAM_Addr_Reg_Pass_through_27, RAM_Addr_Reg_Temp_Enable_2,
       RAM_Addr_Reg_Temp_Enable_4, RAM_Addr_Reg_Temp_Enable_6, RAM_Addr_Reg_Temp_Enable_8,
       RAM_Addr_Reg_Temp_Enable_12, RAM_Addr_Reg_Temp_Enable_25, RAM_Addr_Reg_Temp_Use_2,
       RAM_Addr_Reg_Temp_Use_4, RAM_Addr_Reg_Temp_Use_6, RAM_Addr_Reg_Temp_Use_8, RAM_Addr_Reg_Temp_Use_12,
       RAM_Addr_Reg_Temp_Use_25, RAM_Data_Reg_Pass_through_1, RAM_Data_Reg_Pass_through_2,
       RAM_Data_Reg_Pass_through_3, RAM_Data_Reg_Pass_through_4, RAM_Data_Reg_Pass_through_5,
       RAM_Data_Reg_Pass_through_6, RAM_Data_Reg_Pass_through_7, RAM_Data_Reg_Pass_through_8,
       RAM_Data_Reg_Pass_through_9, RAM_Data_Reg_Pass_through_23, RAM_Data_Reg_Pass_through_24,
       RAM_Data_Reg_Pass_through_25, RAM_Data_Reg_Pass_through_26, RAM_Write_Data_1, RAM_Write_Data_2,
       RAM_Write_Data_3, RAM_Write_Data_4, RAM_Write_Data_5, RAM_Write_Data_6, RAM_Write_Data_7,
       RAM_Write_Data_8, RAM_Write_Data_9, RAM_Write_Data_12, RAM_Write_Data_13, RAM_Write_Data_23,
       RAM_Write_Data_24, RAM_Write_Data_25, RAM_Write_Data_26, State_Input_0, State_Input_1, State_Input_14,
       State_Input_15, State_Input_16, State_Input_17, State_Input_18, State_Input_19, State_Input_20,
       State_Input_21, State_Input_22, State_Input_23, State_Input_24, State_Input_27;
  wire [1:0] ALU_I1_Reg_Sel_2, ALU_I1_Reg_Sel_3, ALU_I1_Reg_Sel_4, ALU_I1_Reg_Sel_5, ALU_I1_Reg_Sel_6,
       ALU_I1_Reg_Sel_7, ALU_I1_Reg_Sel_8, ALU_I1_Reg_Sel_9, ALU_I1_Reg_Sel_10, ALU_I1_Reg_Sel_11,
       ALU_I1_Reg_Sel_25, ALU_I1_Reg_Sel_26, RAM_Data_Reg_Sel_0, RAM_Data_Reg_Sel_1, RAM_Data_Reg_Sel_2,
       RAM_Data_Reg_Sel_3, RAM_Data_Reg_Sel_4, RAM_Data_Reg_Sel_5, RAM_Data_Reg_Sel_6, RAM_Data_Reg_Sel_7,
       RAM_Data_Reg_Sel_8, RAM_Data_Reg_Sel_9, RAM_Data_Reg_Sel_12, RAM_Data_Reg_Sel_13, RAM_Data_Reg_Sel_23,
       RAM_Data_Reg_Sel_24, RAM_Data_Reg_Sel_25, RAM_Data_Reg_Sel_26;
  wire [2:0] ALU_Mode_2, ALU_Mode_3, ALU_Mode_4, ALU_Mode_5, ALU_Mode_7, ALU_Mode_8, ALU_Mode_9, ALU_Mode_23,
       ALU_Mode_24, ALU_Mode_25, ALU_Mode_26, Cond_JMP_Mode_15, Cond_JMP_Mode_16, Cond_JMP_Mode_17,
       Cond_JMP_Mode_18, Cond_JMP_Mode_19, Cond_JMP_Mode_20, Cond_JMP_Mode_21, Cond_JMP_Mode_22;

  CU_00_pass__mem cu_00_pass_mem_1 (
    .Instruction(Instruction), .State(State), .RAM_Data_Reg_Sel(RAM_Data_Reg_Sel_0),
    .ALU_I0_Reg_Enable(ALU_I0_Reg_Enable_0), .ALU_Pass_Through_I0(ALU_Pass_Through_I0),
    .State_Input(State_Input_0), .RAM_Addr_Reg_Pass_through(RAM_Addr_Reg_Pass_through_0));
  CU_01_not__mem cu_01_not_mem_1 (
    .Instruction(Instruction), .State(State), .RAM_Addr_Reg_Pass_through(RAM_Addr_Reg_Pass_through_1),
    .RAM_Data_Reg_Sel(RAM_Data_Reg_Sel_1), .RAM_Write_Data(RAM_Write_Data_1),
    .RAM_Data_Reg_Pass_through(RAM_Data_Reg_Pass_through_1), .State_Input(State_Input_1),
    .ALU_I0_Reg_Enable(ALU_I0_Reg_Enable_1));
  CU_02_or__mem___mem cu_02_or_mem_mem_1 (
    .Instruction(Instruction), .State(State), .RAM_Addr_Reg_Pass_through(RAM_Addr_Reg_Pass_through_2),
    .RAM_Data_Reg_Sel(RAM_Data_Reg_Sel_2), .RAM_Write_Data(RAM_Write_Data_2),
    .RAM_Addr_Reg_Temp_Enable(RAM_Addr_Reg_Temp_Enable_2), .RAM_Addr_Reg_Temp_Use(RAM_Addr_Reg_Temp_Use_2),
    .ALU_I0_Reg_Enable(ALU_I0_Reg_Enable_2), .ALU_I1_Reg_Sel(ALU_I1_Reg_Sel_2), .ALU_Mode(ALU_Mode_2),
    .RAM_Data_Reg_Pass_through(RAM_Data_Reg_Pass_through_2));
  CU_03_or__mem___con cu_03_or_mem_con_1 (
    .Instruction(Instruction), .State(State), .RAM_Addr_Reg_Pass_through(RAM_Addr_Reg_Pass_through_3),
    .RAM_Data_Reg_Pass_through(RAM_Data_Reg_Pass_through_3), .RAM_Data_Reg_Sel(RAM_Data_Reg_Sel_3),
    .RAM_Write_Data(RAM_Write_Data_3), .ALU_I0_Reg_Enable(ALU_I0_Reg_Enable_3),
    .ALU_I1_Reg_Sel(ALU_I1_Reg_Sel_3), .ALU_Mode(ALU_Mode_3));
  CU_04_and__mem___mem cu_04_and_mem_mem_1 (
    .Instruction(Instruction), .State(State), .RAM_Addr_Reg_Pass_through(RAM_Addr_Reg_Pass_through_4),
    .RAM_Data_Reg_Pass_through(RAM_Data_Reg_Pass_through_4), .RAM_Data_Reg_Sel(RAM_Data_Reg_Sel_4),
    .RAM_Write_Data(RAM_Write_Data_4), .RAM_Addr_Reg_Temp_Enable(RAM_Addr_Reg_Temp_Enable_4),
    .RAM_Addr_Reg_Temp_Use(RAM_Addr_Reg_Temp_Use_4), .ALU_I0_Reg_Enable(ALU_I0_Reg_Enable_4),
    .ALU_I1_Reg_Sel(ALU_I1_Reg_Sel_4), .ALU_Mode(ALU_Mode_4));
  CU_05_and__mem___con cu_05_and_mem_con_1 (
    .Instruction(Instruction), .State(State), .RAM_Addr_Reg_Pass_through(RAM_Addr_Reg_Pass_through_5),
    .RAM_Data_Reg_Pass_through(RAM_Data_Reg_Pass_through_5), .RAM_Data_Reg_Sel(RAM_Data_Reg_Sel_5),
    .RAM_Write_Data(RAM_Write_Data_5), .ALU_I0_Reg_Enable(ALU_I0_Reg_Enable_5),
    .ALU_I1_Reg_Sel(ALU_I1_Reg_Sel_5), .ALU_Mode(ALU_Mode_5));
  CU_06_add__mem___mem cu_06_add_mem_mem_1 (
    .Instruction(Instruction), .State(State), .RAM_Addr_Reg_Pass_through(RAM_Addr_Reg_Pass_through_6),
    .RAM_Data_Reg_Pass_through(RAM_Data_Reg_Pass_through_6), .RAM_Data_Reg_Sel(RAM_Data_Reg_Sel_6),
    .RAM_Write_Data(RAM_Write_Data_6), .RAM_Addr_Reg_Temp_Enable(RAM_Addr_Reg_Temp_Enable_6),
    .RAM_Addr_Reg_Temp_Use(RAM_Addr_Reg_Temp_Use_6), .ALU_I0_Reg_Enable(ALU_I0_Reg_Enable_6),
    .ALU_I1_Reg_Sel(ALU_I1_Reg_Sel_6), .ALU_Arith_Logic(ALU_Arith_Logic_6));  // open: ALU_Mode
  CU_07_add__mem___con cu_07_add_mem_con_1 (
    .Instruction(Instruction), .State(State), .RAM_Addr_Reg_Pass_through(RAM_Addr_Reg_Pass_through_7),
    .RAM_Data_Reg_Sel(RAM_Data_Reg_Sel_7), .RAM_Write_Data(RAM_Write_Data_7),
    .ALU_I0_Reg_Enable(ALU_I0_Reg_Enable_7), .ALU_I1_Reg_Sel(ALU_I1_Reg_Sel_7),
    .ALU_Arith_Logic(ALU_Arith_Logic_7), .ALU_Mode(ALU_Mode_7),
    .RAM_Data_Reg_Pass_through(RAM_Data_Reg_Pass_through_7));
  CU_08_sub__mem___mem cu_08_sub_mem_mem_1 (
    .Instruction(Instruction), .State(State), .RAM_Addr_Reg_Pass_through(RAM_Addr_Reg_Pass_through_8),
    .RAM_Data_Reg_Pass_through(RAM_Data_Reg_Pass_through_8), .RAM_Data_Reg_Sel(RAM_Data_Reg_Sel_8),
    .RAM_Write_Data(RAM_Write_Data_8), .RAM_Addr_Reg_Temp_Enable(RAM_Addr_Reg_Temp_Enable_8),
    .RAM_Addr_Reg_Temp_Use(RAM_Addr_Reg_Temp_Use_8), .ALU_I0_Reg_Enable(ALU_I0_Reg_Enable_8),
    .ALU_I1_Reg_Sel(ALU_I1_Reg_Sel_8), .ALU_Arith_Logic(ALU_Arith_Logic_8), .ALU_Mode(ALU_Mode_8));
  CU_09_sub__mem___con cu_09_sub_mem_con_1 (
    .Instruction(Instruction), .State(State), .RAM_Addr_Reg_Pass_through(RAM_Addr_Reg_Pass_through_9),
    .RAM_Data_Reg_Sel(RAM_Data_Reg_Sel_9), .RAM_Write_Data(RAM_Write_Data_9),
    .RAM_Data_Reg_Pass_through(RAM_Data_Reg_Pass_through_9), .ALU_I0_Reg_Enable(ALU_I0_Reg_Enable_9),
    .ALU_I1_Reg_Sel(ALU_I1_Reg_Sel_9), .ALU_Arith_Logic(ALU_Arith_Logic_9), .ALU_Mode(ALU_Mode_9));
  CU_10_cmp__mem___mem cu_10_cmp_mem_mem_1 (
    .Instruction(Instruction), .State(State), .RAM_Addr_Reg_Pass_through(RAM_Addr_Reg_Pass_through_10),
    .ALU_I0_Reg_Enable(ALU_I0_Reg_Enable_10), .ALU_I1_Reg_Sel(ALU_I1_Reg_Sel_10), .ALU_CMP(ALU_CMP_10));
  CU_11_cmp__mem___con cu_11_cmp_mem_con_1 (
    .Instruction(Instruction), .State(State), .RAM_Addr_Reg_Pass_through(RAM_Addr_Reg_Pass_through_11),
    .ALU_I0_Reg_Enable(ALU_I0_Reg_Enable_11), .ALU_I1_Reg_Sel(ALU_I1_Reg_Sel_11), .ALU_CMP(ALU_CMP_11));
  CU_12_mov__mem___mem cu_12_mov_mem_mem_1 (
    .Instruction(Instruction), .State(State), .RAM_Addr_Reg_Pass_through(RAM_Addr_Reg_Pass_through_12),
    .RAM_Data_Reg_Sel(RAM_Data_Reg_Sel_12), .RAM_Write_Data(RAM_Write_Data_12),
    .RAM_Addr_Reg_Temp_Enable(RAM_Addr_Reg_Temp_Enable_12), .RAM_Addr_Reg_Temp_Use(RAM_Addr_Reg_Temp_Use_12));
  CU_13_mov__mem___con cu_13_mov_mem_con_1 (
    .Instruction(Instruction), .State(State), .RAM_Addr_Reg_Enable(RAM_Addr_Reg_Enable),
    .RAM_Data_Reg_Sel(RAM_Data_Reg_Sel_13), .RAM_Write_Data(RAM_Write_Data_13));
  not not_1 (not_1_out, State[1]);
  not not_2 (not_2_out, State[2]);
  not not_3 (not_3_out, State[0]);
  and and_1 (IR_Load, not_3_out, not_1_out, not_2_out);
  and and_2 (and_2_out, not_3_out, State[1], not_2_out);
  or or_1 (IP_plus_plus, IR_Load, and_2_out, and_3_out);
  and and_3 (and_3_out, State[0], State[1], not_2_out);
  and and_4 (Cond_JMP_Reg_Enable, not_3_out, not_1_out, State[2]);
  CU_14_jmp__label cu_14_jmp_label_1 (
    .Instruction(Instruction), .State(State), .Enable_JMP(Enable_JMP), .State_Input(State_Input_14),
    .JMP_Reg_Enable(JMP_Reg_Enable_14));
  CU_15_je__label cu_15_je_label_1 (
    .Instruction(Instruction), .State(State), .Cond_JMP_Enable(Cond_JMP_Enable_15),
    .Cond_JMP_Mode(Cond_JMP_Mode_15), .JMP_Reg_Enable(JMP_Reg_Enable_15), .State_Input(State_Input_15));
  CU_16_jne__label cu_16_jne_label_1 (
    .Instruction(Instruction), .State(State), .Cond_JMP_Enable(Cond_JMP_Enable_16),
    .Cond_JMP_Mode(Cond_JMP_Mode_16), .JMP_Reg_Enable(JMP_Reg_Enable_16), .State_Input(State_Input_16));
  CU_17_jg__label cu_17_jg_label_1 (
    .Instruction(Instruction), .State(State), .Cond_JMP_Enable(Cond_JMP_Enable_17),
    .Cond_JMP_Mode(Cond_JMP_Mode_17), .JMP_Reg_Enable(JMP_Reg_Enable_17), .State_Input(State_Input_17));
  CU_18_jge__label cu_18_jge_label_1 (
    .Instruction(Instruction), .State(State), .Cond_JMP_Enable(Cond_JMP_Enable_18),
    .Cond_JMP_Mode(Cond_JMP_Mode_18), .JMP_Reg_Enable(JMP_Reg_Enable_18), .State_Input(State_Input_18));
  CU_19_jl__label cu_19_jl_label_1 (
    .Instruction(Instruction), .State(State), .Cond_JMP_Enable(Cond_JMP_Enable_19),
    .Cond_JMP_Mode(Cond_JMP_Mode_19), .JMP_Reg_Enable(JMP_Reg_Enable_19), .State_Input(State_Input_19));
  CU_20_jle__label cu_20_jle_label_1 (
    .Instruction(Instruction), .State(State), .Cond_JMP_Enable(Cond_JMP_Enable_20),
    .Cond_JMP_Mode(Cond_JMP_Mode_20), .JMP_Reg_Enable(JMP_Reg_Enable_20), .State_Input(State_Input_20));
  CU_21_jz__label cu_21_jz_label_1 (
    .Instruction(Instruction), .State(State), .Cond_JMP_Enable(Cond_JMP_Enable_21),
    .Cond_JMP_Mode(Cond_JMP_Mode_21), .JMP_Reg_Enable(JMP_Reg_Enable_21), .State_Input(State_Input_21));
  CU_22_jnz__label cu_22_jnz_label_1 (
    .Instruction(Instruction), .State(State), .Cond_JMP_Enable(Cond_JMP_Enable_22),
    .Cond_JMP_Mode(Cond_JMP_Mode_22), .JMP_Reg_Enable(JMP_Reg_Enable_22), .State_Input(State_Input_22));
  assign RAM_Data_Reg_Sel = RAM_Data_Reg_Sel_23 | RAM_Data_Reg_Sel_25 | RAM_Data_Reg_Sel_8 | RAM_Data_Reg_Sel_9 | RAM_Data_Reg_Sel_6 | RAM_Data_Reg_Sel_3 | RAM_Data_Reg_Sel_2 | RAM_Data_Reg_Sel_7 | RAM_Data_Reg_Sel_13 | RAM_Data_Reg_Sel_0 | RAM_Data_Reg_Sel_24 | RAM_Data_Reg_Sel_1 | RAM_Data_Reg_Sel_5 | RAM_Data_Reg_Sel_4 | RAM_Data_Reg_Sel_12 | RAM_Data_Reg_Sel_26;  // OR_Gate or_2, 2 bits wide
  or or_3 (RAM_Write_Data, RAM_Write_Data_25, RAM_Write_Data_8, RAM_Write_Data_9, RAM_Write_Data_6, RAM_Write_Data_3, RAM_Write_Data_7, RAM_Write_Data_13, RAM_Write_Data_24, RAM_Write_Data_1, RAM_Write_Data_2, RAM_Write_Data_4, RAM_Write_Data_5, RAM_Write_Data_12, RAM_Write_Data_23, RAM_Write_Data_26);
  or or_4 (RAM_Addr_Reg_Temp_Use, RAM_Addr_Reg_Temp_Use_12, RAM_Addr_Reg_Temp_Use_8, RAM_Addr_Reg_Temp_Use_6, RAM_Addr_Reg_Temp_Use_2, RAM_Addr_Reg_Temp_Use_4, RAM_Addr_Reg_Temp_Use_25);
  assign ALU_I1_Reg_Sel = ALU_I1_Reg_Sel_8 | ALU_I1_Reg_Sel_9 | ALU_I1_Reg_Sel_6 | ALU_I1_Reg_Sel_3 | ALU_I1_Reg_Sel_2 | ALU_I1_Reg_Sel_7 | ALU_I1_Reg_Sel_11 | ALU_I1_Reg_Sel_4 | ALU_I1_Reg_Sel_5 | ALU_I1_Reg_Sel_10 | ALU_I1_Reg_Sel_25 | ALU_I1_Reg_Sel_26;  // OR_Gate or_5, 2 bits wide
  or or_6 (ALU_CMP, ALU_CMP_10, ALU_CMP_11);
  or or_7 (Cond_JMP_Enable, Cond_JMP_Enable_19, Cond_JMP_Enable_20, Cond_JMP_Enable_21, Cond_JMP_Enable_15, Cond_JMP_Enable_22, Cond_JMP_Enable_16, Cond_JMP_Enable_17, Cond_JMP_Enable_18);
  or or_8 (JMP_Reg_Enable, JMP_Reg_Enable_19, JMP_Reg_Enable_20, JMP_Reg_Enable_22, JMP_Reg_Enable_21, JMP_Reg_Enable_14, JMP_Reg_Enable_15, JMP_Reg_Enable_16, JMP_Reg_Enable_17, JMP_Reg_Enable_18);
  CU_23_inc__mem cu_23_inc_mem_1 (
    .Instruction(Instruction), .State(State), .RAM_Addr_Reg_Pass_through(RAM_Addr_Reg_Pass_through_23),
    .RAM_Data_Reg_Sel(RAM_Data_Reg_Sel_23), .RAM_Write_Data(RAM_Write_Data_23),
    .RAM_Data_Reg_Pass_through(RAM_Data_Reg_Pass_through_23), .State_Input(State_Input_23),
    .ALU_I0_Reg_Enable(ALU_I0_Reg_Enable_23), .ALU_Arith_Logic(ALU_Arith_Logic_23), .ALU_Mode(ALU_Mode_23));
  CU_24_dec__mem cu_24_dec_mem_1 (
    .Instruction(Instruction), .State(State), .RAM_Addr_Reg_Pass_through(RAM_Addr_Reg_Pass_through_24),
    .RAM_Data_Reg_Sel(RAM_Data_Reg_Sel_24), .RAM_Write_Data(RAM_Write_Data_24),
    .RAM_Data_Reg_Pass_through(RAM_Data_Reg_Pass_through_24), .State_Input(State_Input_24),
    .ALU_I0_Reg_Enable(ALU_I0_Reg_Enable_24), .ALU_Arith_Logic(ALU_Arith_Logic_24), .ALU_Mode(ALU_Mode_24));
  CU_25_xor__mem___mem cu_25_xor_mem_mem_1 (
    .Instruction(Instruction), .State(State), .RAM_Addr_Reg_Pass_through(RAM_Addr_Reg_Pass_through_25),
    .RAM_Data_Reg_Pass_through(RAM_Data_Reg_Pass_through_25), .RAM_Data_Reg_Sel(RAM_Data_Reg_Sel_25),
    .RAM_Write_Data(RAM_Write_Data_25), .RAM_Addr_Reg_Temp_Enable(RAM_Addr_Reg_Temp_Enable_25),
    .RAM_Addr_Reg_Temp_Use(RAM_Addr_Reg_Temp_Use_25), .ALU_I0_Reg_Enable(ALU_I0_Reg_Enable_25),
    .ALU_I1_Reg_Sel(ALU_I1_Reg_Sel_25), .ALU_Mode(ALU_Mode_25));
  CU_26_xor__mem___con cu_26_xor_mem_con_1 (
    .Instruction(Instruction), .State(State), .RAM_Addr_Reg_Pass_through(RAM_Addr_Reg_Pass_through_26),
    .RAM_Data_Reg_Pass_through(RAM_Data_Reg_Pass_through_26), .RAM_Data_Reg_Sel(RAM_Data_Reg_Sel_26),
    .RAM_Write_Data(RAM_Write_Data_26), .ALU_I0_Reg_Enable(ALU_I0_Reg_Enable_26),
    .ALU_I1_Reg_Sel(ALU_I1_Reg_Sel_26), .ALU_Mode(ALU_Mode_26));
  CU_27_out__mem cu_27_out_mem_1 (
    .Instruction(Instruction), .State(State), .RAM_Addr_Reg_Pass_through(RAM_Addr_Reg_Pass_through_27),
    .State_Input(State_Input_27), .Output_Reg_Enable(Output_Reg_Enable));
  or or_9 (RAM_Addr_Reg_Pass_through, RAM_Addr_Reg_Pass_through_25, RAM_Addr_Reg_Pass_through_23, RAM_Addr_Reg_Pass_through_12, RAM_Addr_Reg_Pass_through_8, RAM_Addr_Reg_Pass_through_9, RAM_Addr_Reg_Pass_through_7, RAM_Addr_Reg_Pass_through_1, RAM_Addr_Reg_Pass_through_27, RAM_Addr_Reg_Pass_through_11, RAM_Addr_Reg_Pass_through_7, RAM_Addr_Reg_Pass_through_24, RAM_Addr_Reg_Pass_through_0, RAM_Addr_Reg_Pass_through_2, RAM_Addr_Reg_Pass_through_3, RAM_Addr_Reg_Pass_through_4, RAM_Addr_Reg_Pass_through_5, RAM_Addr_Reg_Pass_through_10, RAM_Addr_Reg_Pass_through_26, RAM_Addr_Reg_Pass_through_6);
  or or_10 (RAM_Data_Reg_Pass_through, RAM_Data_Reg_Pass_through_23, RAM_Data_Reg_Pass_through_8, RAM_Data_Reg_Pass_through_9, RAM_Data_Reg_Pass_through_6, RAM_Data_Reg_Pass_through_3, RAM_Data_Reg_Pass_through_2, RAM_Data_Reg_Pass_through_7, RAM_Data_Reg_Pass_through_24, RAM_Data_Reg_Pass_through_1, RAM_Data_Reg_Pass_through_4, RAM_Data_Reg_Pass_through_5, RAM_Data_Reg_Pass_through_25, RAM_Data_Reg_Pass_through_26);
  or or_11 (RAM_Addr_Reg_Temp_Enable, RAM_Addr_Reg_Temp_Enable_12, RAM_Addr_Reg_Temp_Enable_8, RAM_Addr_Reg_Temp_Enable_2, RAM_Addr_Reg_Temp_Enable_4, RAM_Addr_Reg_Temp_Enable_6, RAM_Addr_Reg_Temp_Enable_25);
  or or_12 (ALU_I0_Reg_Enable, ALU_I0_Reg_Enable_23, ALU_I0_Reg_Enable_25, ALU_I0_Reg_Enable_8, ALU_I0_Reg_Enable_9, ALU_I0_Reg_Enable_6, ALU_I0_Reg_Enable_2, ALU_I0_Reg_Enable_1, ALU_I0_Reg_Enable_0, ALU_I0_Reg_Enable_7, ALU_I0_Reg_Enable_11, ALU_I0_Reg_Enable_24, ALU_I0_Reg_Enable_3, ALU_I0_Reg_Enable_4, ALU_I0_Reg_Enable_5, ALU_I0_Reg_Enable_10, ALU_I0_Reg_Enable_26);
  or or_13 (ALU_Arith_Logic, ALU_Arith_Logic_23, ALU_Arith_Logic_6, ALU_Arith_Logic_7, ALU_Arith_Logic_24, ALU_Arith_Logic_9, ALU_Arith_Logic_8);
  assign ALU_Mode = ALU_Mode_25 | ALU_Mode_26 | ALU_Mode_4 | ALU_Mode_5 | ALU_Mode_2 | ALU_Mode_7 | ALU_Mode_24 | ALU_Mode_3 | ALU_Mode_7 | ALU_Mode_8 | ALU_Mode_23 | ALU_Mode_9;  // OR_Gate or_14, 3 bits wide
  assign Cond_JMP_Mode = Cond_JMP_Mode_16 | Cond_JMP_Mode_17 | Cond_JMP_Mode_18 | Cond_JMP_Mode_21 | Cond_JMP_Mode_15 | Cond_JMP_Mode_22 | Cond_JMP_Mode_19 | Cond_JMP_Mode_20;  // OR_Gate or_15, 3 bits wide
  or or_16 (State_Input, State_Input_16, State_Input_17, State_Input_1, State_Input_27, State_Input_21, State_Input_15, State_Input_0, State_Input_14, State_Input_24, State_Input_22, State_Input_18, State_Input_19, State_Input_20, State_Input_23);

  // Other names for the same wires on the sheet: ALU_Pass_Through_I0_0 = ALU_Pass_Through_I0;
  //   Enable_JMP_14 = Enable_JMP; Instruction_CU[4:0] = Instruction; Output_Reg_Enable_27 = Output_Reg_Enable;
  //   RAM_Addr_Reg_Enable_13 = RAM_Addr_Reg_Enable; State_CU[2:0] = State

  // Notes on the sheet:
  //   State_Input: pull=down
endmodule

module CU_00_pass__mem (
  input  [4:0] Instruction,
  input  [2:0] State,
  output RAM_Addr_Reg_Pass_through,
  output [1:0] RAM_Data_Reg_Sel,
  output ALU_I0_Reg_Enable,
  output ALU_Pass_Through_I0,
  output State_Input
);

  wire and_2_out, and_3_out, and_4_out, and_5_out, not_1_out, not_2_out, not_3_out, not_4_out, not_5_out,
       not_6_out, not_7_out, not_8_out;
  wire [2:2] and_1_out;

  not not_1 (not_1_out, Instruction[0]);
  not not_2 (not_2_out, Instruction[1]);
  not not_3 (not_3_out, Instruction[2]);
  not not_4 (not_4_out, Instruction[3]);
  not not_5 (not_5_out, Instruction[4]);
  and and_1 (and_1_out[2], not_1_out, not_2_out, not_3_out, not_4_out, not_5_out);
  not not_6 (not_6_out, State[1]);
  not not_7 (not_7_out, State[2]);
  not not_8 (not_8_out, State[0]);
  and and_2 (and_2_out, not_8_out, State[1], not_7_out);
  and and_3 (and_3_out, State[0], State[1], not_7_out);
  and and_4 (and_4_out, not_8_out, not_6_out, State[2]);
  and and_5 (and_5_out, State[0], not_6_out, not_7_out);
  and and_6 (RAM_Addr_Reg_Pass_through, and_1_out[2], and_3_out);
  assign RAM_Data_Reg_Sel = {2{and_1_out[2]}};  // AND_Gate and_7, 2 bits wide AND_Gate
  and and_8 (ALU_I0_Reg_Enable, and_1_out[2], and_3_out);
  and and_9 (ALU_Pass_Through_I0, and_1_out[2], and_4_out);
  and and_10 (State_Input, and_1_out[2], and_5_out);

  // Notes on the sheet:
  //   State_Input: pull=down
  //   S2
  //   S3
  //   S4
  //   S1
endmodule

module CU_01_not__mem (
  input  [4:0] Instruction,
  input  [2:0] State,
  output RAM_Addr_Reg_Pass_through,
  output [1:0] RAM_Data_Reg_Sel,
  output RAM_Write_Data,
  output RAM_Data_Reg_Pass_through,
  output State_Input,
  output ALU_I0_Reg_Enable
);

  wire and_2_out, and_3_out, and_5_out, not_1_out, not_2_out, not_3_out, not_4_out, not_5_out, not_6_out,
       not_7_out;
  wire [1:1] and_4_out;
  wire [2:2] and_1_out;

  not not_1 (not_1_out, Instruction[1]);
  not not_2 (not_2_out, Instruction[2]);
  not not_3 (not_3_out, Instruction[3]);
  not not_4 (not_4_out, Instruction[4]);
  and and_1 (and_1_out[2], Instruction[0], not_1_out, not_2_out, not_3_out, not_4_out);
  not not_5 (not_5_out, State[1]);
  not not_6 (not_6_out, State[2]);
  not not_7 (not_7_out, State[0]);
  and and_2 (and_2_out, not_7_out, State[1], not_6_out);
  and and_3 (and_3_out, State[0], State[1], not_6_out);
  and and_4 (and_4_out[1], not_7_out, not_5_out, State[2]);
  and and_5 (and_5_out, State[0], not_5_out, not_6_out);
  and and_6 (RAM_Addr_Reg_Pass_through, and_1_out[2], and_3_out);
  assign RAM_Data_Reg_Sel = {2{and_1_out[2]}} & {and_4_out[1], 1'b0};  // AND_Gate and_7, 2 bits wide
  and and_8 (RAM_Write_Data, and_1_out[2], and_4_out[1]);
  and and_9 (RAM_Data_Reg_Pass_through, and_1_out[2], and_4_out[1]);
  and and_10 (State_Input, and_1_out[2], and_5_out);
  and and_11 (ALU_I0_Reg_Enable, and_1_out[2], and_3_out);

  // Notes on the sheet:
  //   State_Input: pull=down
  //   S2
  //   S3
  //   S4
  //   S1
endmodule

module CU_02_or__mem___mem (
  input  [4:0] Instruction,
  input  [2:0] State,
  output RAM_Addr_Reg_Pass_through,
  output RAM_Data_Reg_Pass_through,
  output [1:0] RAM_Data_Reg_Sel,
  output RAM_Write_Data,
  output RAM_Addr_Reg_Temp_Enable,
  output RAM_Addr_Reg_Temp_Use,
  output ALU_I0_Reg_Enable,
  output [1:0] ALU_I1_Reg_Sel,
  output [2:0] ALU_Mode
);

  wire and_2_out, and_5_out, and_6_out, not_1_out, not_2_out, not_3_out, not_4_out, not_5_out, not_6_out,
       not_7_out;
  wire [1:1] and_3_out, and_4_out;
  wire [2:2] and_1_out;

  not not_1 (not_1_out, Instruction[0]);
  not not_2 (not_2_out, Instruction[2]);
  not not_3 (not_3_out, Instruction[3]);
  not not_4 (not_4_out, Instruction[4]);
  and and_1 (and_1_out[2], not_1_out, Instruction[1], not_2_out, not_3_out, not_4_out);
  not not_5 (not_5_out, State[1]);
  not not_6 (not_6_out, State[2]);
  not not_7 (not_7_out, State[0]);
  and and_2 (and_2_out, not_7_out, State[1], not_6_out);
  and and_3 (and_3_out[1], State[0], State[1], not_6_out);
  and and_4 (and_4_out[1], not_7_out, not_5_out, State[2]);
  and and_5 (and_5_out, and_1_out[2], and_2_out);
  and and_6 (and_6_out, and_1_out[2], and_3_out[1]);
  and and_7 (RAM_Data_Reg_Pass_through, and_1_out[2], and_4_out[1]);
  assign RAM_Data_Reg_Sel = {2{and_1_out[2]}} & {and_4_out[1], 1'b0};  // AND_Gate and_8, 2 bits wide
  and and_9 (RAM_Write_Data, and_1_out[2], and_4_out[1]);
  and and_10 (RAM_Addr_Reg_Temp_Enable, and_1_out[2], and_2_out);
  and and_11 (RAM_Addr_Reg_Temp_Use, and_1_out[2], and_4_out[1]);
  and and_12 (ALU_I0_Reg_Enable, and_1_out[2], and_2_out);
  assign ALU_I1_Reg_Sel = {2{and_1_out[2]}} & {and_3_out[1], 1'b0};  // AND_Gate and_13, 2 bits wide
  assign ALU_Mode = {3{and_1_out[2]}} & {2'b00, and_4_out[1]};  // AND_Gate and_14, 3 bits wide
  or or_1 (RAM_Addr_Reg_Pass_through, and_5_out, and_6_out);

  // Notes on the sheet:
  //   S2
  //   S3
  //   S4
endmodule

module CU_03_or__mem___con (
  input  [4:0] Instruction,
  input  [2:0] State,
  output RAM_Addr_Reg_Pass_through,
  output RAM_Data_Reg_Pass_through,
  output [1:0] RAM_Data_Reg_Sel,
  output RAM_Write_Data,
  output ALU_I0_Reg_Enable,
  output [1:0] ALU_I1_Reg_Sel,
  output [2:0] ALU_Mode
);

  wire and_2_out, not_1_out, not_2_out, not_3_out, not_4_out, not_5_out, not_6_out;
  wire [0:0] and_3_out;
  wire [1:1] and_4_out;
  wire [2:2] and_1_out;

  not not_1 (not_1_out, Instruction[2]);
  not not_2 (not_2_out, Instruction[3]);
  not not_3 (not_3_out, Instruction[4]);
  and and_1 (and_1_out[2], Instruction[0], Instruction[1], not_1_out, not_2_out, not_3_out);
  not not_4 (not_4_out, State[1]);
  not not_5 (not_5_out, State[2]);
  not not_6 (not_6_out, State[0]);
  and and_2 (and_2_out, not_6_out, State[1], not_5_out);
  and and_3 (and_3_out[0], State[0], State[1], not_5_out);
  and and_4 (and_4_out[1], not_6_out, not_4_out, State[2]);
  and and_5 (RAM_Addr_Reg_Pass_through, and_1_out[2], and_2_out);
  and and_6 (RAM_Data_Reg_Pass_through, and_1_out[2], and_4_out[1]);
  assign RAM_Data_Reg_Sel = {2{and_1_out[2]}} & {and_4_out[1], 1'b0};  // AND_Gate and_7, 2 bits wide
  and and_8 (RAM_Write_Data, and_1_out[2], and_4_out[1]);
  and and_9 (ALU_I0_Reg_Enable, and_1_out[2], and_2_out);
  assign ALU_I1_Reg_Sel = {2{and_1_out[2]}} & {1'b0, and_3_out[0]};  // AND_Gate and_10, 2 bits wide
  assign ALU_Mode = {3{and_1_out[2]}} & {2'b00, and_4_out[1]};  // AND_Gate and_11, 3 bits wide

  // Notes on the sheet:
  //   S2
  //   S3
  //   S4
endmodule

module CU_04_and__mem___mem (
  input  [4:0] Instruction,
  input  [2:0] State,
  output RAM_Addr_Reg_Pass_through,
  output RAM_Data_Reg_Pass_through,
  output [1:0] RAM_Data_Reg_Sel,
  output RAM_Write_Data,
  output RAM_Addr_Reg_Temp_Enable,
  output RAM_Addr_Reg_Temp_Use,
  output ALU_I0_Reg_Enable,
  output [1:0] ALU_I1_Reg_Sel,
  output [2:0] ALU_Mode
);

  wire and_2_out, and_5_out, and_6_out, not_1_out, not_2_out, not_3_out, not_4_out, not_5_out, not_6_out,
       not_7_out;
  wire [1:1] and_3_out, and_4_out;
  wire [2:2] and_1_out;

  not not_1 (not_1_out, Instruction[0]);
  not not_2 (not_2_out, Instruction[1]);
  not not_3 (not_3_out, Instruction[3]);
  not not_4 (not_4_out, Instruction[4]);
  and and_1 (and_1_out[2], not_1_out, not_2_out, Instruction[2], not_3_out, not_4_out);
  not not_5 (not_5_out, State[1]);
  not not_6 (not_6_out, State[2]);
  not not_7 (not_7_out, State[0]);
  and and_2 (and_2_out, not_7_out, State[1], not_6_out);
  and and_3 (and_3_out[1], State[0], State[1], not_6_out);
  and and_4 (and_4_out[1], not_7_out, not_5_out, State[2]);
  and and_5 (and_5_out, and_1_out[2], and_2_out);
  and and_6 (and_6_out, and_1_out[2], and_3_out[1]);
  and and_7 (RAM_Data_Reg_Pass_through, and_1_out[2], and_4_out[1]);
  assign RAM_Data_Reg_Sel = {2{and_1_out[2]}} & {and_4_out[1], 1'b0};  // AND_Gate and_8, 2 bits wide
  and and_9 (RAM_Write_Data, and_1_out[2], and_4_out[1]);
  and and_10 (RAM_Addr_Reg_Temp_Enable, and_1_out[2], and_2_out);
  and and_11 (RAM_Addr_Reg_Temp_Use, and_1_out[2], and_4_out[1]);
  and and_12 (ALU_I0_Reg_Enable, and_1_out[2], and_2_out);
  assign ALU_I1_Reg_Sel = {2{and_1_out[2]}} & {and_3_out[1], 1'b0};  // AND_Gate and_13, 2 bits wide
  assign ALU_Mode = {3{and_1_out[2]}} & {1'b0, and_4_out[1], 1'b0};  // AND_Gate and_14, 3 bits wide
  or or_1 (RAM_Addr_Reg_Pass_through, and_5_out, and_6_out);

  // Notes on the sheet:
  //   S2
  //   S3
  //   S4
endmodule

module CU_05_and__mem___con (
  input  [4:0] Instruction,
  input  [2:0] State,
  output RAM_Addr_Reg_Pass_through,
  output RAM_Data_Reg_Pass_through,
  output [1:0] RAM_Data_Reg_Sel,
  output RAM_Write_Data,
  output ALU_I0_Reg_Enable,
  output [1:0] ALU_I1_Reg_Sel,
  output [2:0] ALU_Mode
);

  wire and_2_out, not_1_out, not_2_out, not_3_out, not_4_out, not_5_out, not_6_out;
  wire [0:0] and_3_out;
  wire [1:1] and_4_out;
  wire [2:2] and_1_out;

  not not_1 (not_1_out, Instruction[1]);
  not not_2 (not_2_out, Instruction[3]);
  not not_3 (not_3_out, Instruction[4]);
  and and_1 (and_1_out[2], Instruction[0], not_1_out, Instruction[2], not_2_out, not_3_out);
  not not_4 (not_4_out, State[1]);
  not not_5 (not_5_out, State[2]);
  not not_6 (not_6_out, State[0]);
  and and_2 (and_2_out, not_6_out, State[1], not_5_out);
  and and_3 (and_3_out[0], State[0], State[1], not_5_out);
  and and_4 (and_4_out[1], not_6_out, not_4_out, State[2]);
  and and_5 (RAM_Addr_Reg_Pass_through, and_1_out[2], and_2_out);
  and and_6 (RAM_Data_Reg_Pass_through, and_1_out[2], and_4_out[1]);
  assign RAM_Data_Reg_Sel = {2{and_1_out[2]}} & {and_4_out[1], 1'b0};  // AND_Gate and_7, 2 bits wide
  and and_8 (RAM_Write_Data, and_1_out[2], and_4_out[1]);
  and and_9 (ALU_I0_Reg_Enable, and_1_out[2], and_2_out);
  assign ALU_I1_Reg_Sel = {2{and_1_out[2]}} & {1'b0, and_3_out[0]};  // AND_Gate and_10, 2 bits wide
  assign ALU_Mode = {3{and_1_out[2]}} & {1'b0, and_4_out[1], 1'b0};  // AND_Gate and_11, 3 bits wide

  // Notes on the sheet:
  //   S2
  //   S3
  //   S4
endmodule

module CU_06_add__mem___mem (
  input  [4:0] Instruction,
  input  [2:0] State,
  output RAM_Addr_Reg_Pass_through,
  output RAM_Data_Reg_Pass_through,
  output [1:0] RAM_Data_Reg_Sel,
  output RAM_Write_Data,
  output RAM_Addr_Reg_Temp_Enable,
  output RAM_Addr_Reg_Temp_Use,
  output ALU_I0_Reg_Enable,
  output [1:0] ALU_I1_Reg_Sel,
  output ALU_Arith_Logic,
  output [2:0] ALU_Mode
);

  wire and_2_out, and_5_out, and_6_out, not_1_out, not_2_out, not_3_out, not_4_out, not_5_out, not_6_out;
  wire [1:1] and_3_out, and_4_out;
  wire [2:2] and_1_out;

  not not_1 (not_1_out, Instruction[0]);
  not not_2 (not_2_out, Instruction[3]);
  not not_3 (not_3_out, Instruction[4]);
  and and_1 (and_1_out[2], not_1_out, Instruction[1], Instruction[2], not_2_out, not_3_out);
  not not_4 (not_4_out, State[1]);
  not not_5 (not_5_out, State[2]);
  not not_6 (not_6_out, State[0]);
  and and_2 (and_2_out, not_6_out, State[1], not_5_out);
  and and_3 (and_3_out[1], State[0], State[1], not_5_out);
  and and_4 (and_4_out[1], not_6_out, not_4_out, State[2]);
  and and_5 (and_5_out, and_1_out[2], and_2_out);
  and and_6 (and_6_out, and_1_out[2], and_3_out[1]);
  and and_7 (RAM_Data_Reg_Pass_through, and_1_out[2], and_4_out[1]);
  assign RAM_Data_Reg_Sel = {2{and_1_out[2]}} & {and_4_out[1], 1'b0};  // AND_Gate and_8, 2 bits wide
  and and_9 (RAM_Write_Data, and_1_out[2], and_4_out[1]);
  and and_10 (RAM_Addr_Reg_Temp_Enable, and_1_out[2], and_2_out);
  and and_11 (RAM_Addr_Reg_Temp_Use, and_1_out[2], and_4_out[1]);
  and and_12 (ALU_I0_Reg_Enable, and_1_out[2], and_2_out);
  assign ALU_I1_Reg_Sel = {2{and_1_out[2]}} & {and_3_out[1], 1'b0};  // AND_Gate and_13, 2 bits wide
  and and_14 (ALU_Arith_Logic, and_1_out[2], and_4_out[1]);
  assign ALU_Mode = {3{and_1_out[2]}} & 3'b000;  // AND_Gate and_15, 3 bits wide
  or or_1 (RAM_Addr_Reg_Pass_through, and_5_out, and_6_out);

  // Notes on the sheet:
  //   S2
  //   S3
  //   S4
endmodule

module CU_07_add__mem___con (
  input  [4:0] Instruction,
  input  [2:0] State,
  output RAM_Addr_Reg_Pass_through,
  output [1:0] RAM_Data_Reg_Sel,
  output RAM_Write_Data,
  output RAM_Data_Reg_Pass_through,
  output ALU_I0_Reg_Enable,
  output [1:0] ALU_I1_Reg_Sel,
  output ALU_Arith_Logic,
  output [2:0] ALU_Mode
);

  wire and_2_out, not_1_out, not_2_out, not_3_out, not_4_out, not_5_out;
  wire [0:0] and_3_out;
  wire [1:1] and_4_out;
  wire [2:2] and_1_out;

  not not_1 (not_1_out, Instruction[3]);
  not not_2 (not_2_out, Instruction[4]);
  and and_1 (and_1_out[2], Instruction[0], Instruction[1], Instruction[2], not_1_out, not_2_out);
  not not_3 (not_3_out, State[1]);
  not not_4 (not_4_out, State[2]);
  not not_5 (not_5_out, State[0]);
  and and_2 (and_2_out, not_5_out, State[1], not_4_out);
  and and_3 (and_3_out[0], State[0], State[1], not_4_out);
  and and_4 (and_4_out[1], not_5_out, not_3_out, State[2]);
  and and_5 (RAM_Addr_Reg_Pass_through, and_1_out[2], and_2_out);
  assign RAM_Data_Reg_Sel = {2{and_1_out[2]}} & {and_4_out[1], 1'b0};  // AND_Gate and_6, 2 bits wide
  and and_7 (RAM_Write_Data, and_1_out[2], and_4_out[1]);
  and and_8 (RAM_Data_Reg_Pass_through, and_1_out[2], and_4_out[1]);
  and and_9 (ALU_I0_Reg_Enable, and_1_out[2], and_2_out);
  assign ALU_I1_Reg_Sel = {2{and_1_out[2]}} & {1'b0, and_3_out[0]};  // AND_Gate and_10, 2 bits wide
  and and_11 (ALU_Arith_Logic, and_1_out[2], and_4_out[1]);
  assign ALU_Mode = {3{and_1_out[2]}} & 3'b000;  // AND_Gate and_12, 3 bits wide

  // Notes on the sheet:
  //   S2
  //   S3
  //   S4
endmodule

module CU_08_sub__mem___mem (
  input  [4:0] Instruction,
  input  [2:0] State,
  output RAM_Addr_Reg_Pass_through,
  output RAM_Data_Reg_Pass_through,
  output [1:0] RAM_Data_Reg_Sel,
  output RAM_Write_Data,
  output RAM_Addr_Reg_Temp_Enable,
  output RAM_Addr_Reg_Temp_Use,
  output ALU_I0_Reg_Enable,
  output [1:0] ALU_I1_Reg_Sel,
  output ALU_Arith_Logic,
  output [2:0] ALU_Mode
);

  wire and_2_out, and_5_out, and_6_out, not_1_out, not_2_out, not_3_out, not_4_out, not_5_out, not_6_out,
       not_7_out;
  wire [1:1] and_3_out, and_4_out;
  wire [2:2] and_1_out;

  not not_1 (not_1_out, Instruction[0]);
  not not_2 (not_2_out, Instruction[1]);
  not not_3 (not_3_out, Instruction[2]);
  not not_4 (not_4_out, Instruction[4]);
  and and_1 (and_1_out[2], not_1_out, not_2_out, not_3_out, Instruction[3], not_4_out);
  not not_5 (not_5_out, State[1]);
  not not_6 (not_6_out, State[2]);
  not not_7 (not_7_out, State[0]);
  and and_2 (and_2_out, not_7_out, State[1], not_6_out);
  and and_3 (and_3_out[1], State[0], State[1], not_6_out);
  and and_4 (and_4_out[1], not_7_out, not_5_out, State[2]);
  and and_5 (and_5_out, and_1_out[2], and_2_out);
  and and_6 (and_6_out, and_1_out[2], and_3_out[1]);
  and and_7 (RAM_Data_Reg_Pass_through, and_1_out[2], and_4_out[1]);
  assign RAM_Data_Reg_Sel = {2{and_1_out[2]}} & {and_4_out[1], 1'b0};  // AND_Gate and_8, 2 bits wide
  and and_9 (RAM_Write_Data, and_1_out[2], and_4_out[1]);
  and and_10 (RAM_Addr_Reg_Temp_Enable, and_1_out[2], and_2_out);
  and and_11 (RAM_Addr_Reg_Temp_Use, and_1_out[2], and_4_out[1]);
  and and_12 (ALU_I0_Reg_Enable, and_1_out[2], and_2_out);
  assign ALU_I1_Reg_Sel = {2{and_1_out[2]}} & {and_3_out[1], 1'b0};  // AND_Gate and_13, 2 bits wide
  and and_14 (ALU_Arith_Logic, and_1_out[2], and_4_out[1]);
  assign ALU_Mode = {3{and_1_out[2]}} & {2'b00, and_4_out[1]};  // AND_Gate and_15, 3 bits wide
  or or_1 (RAM_Addr_Reg_Pass_through, and_5_out, and_6_out);

  // Notes on the sheet:
  //   S2
  //   S3
  //   S4
endmodule

module CU_09_sub__mem___con (
  input  [4:0] Instruction,
  input  [2:0] State,
  output RAM_Addr_Reg_Pass_through,
  output [1:0] RAM_Data_Reg_Sel,
  output RAM_Write_Data,
  output RAM_Data_Reg_Pass_through,
  output ALU_I0_Reg_Enable,
  output [1:0] ALU_I1_Reg_Sel,
  output ALU_Arith_Logic,
  output [2:0] ALU_Mode
);

  wire and_2_out, not_1_out, not_2_out, not_3_out, not_4_out, not_5_out, not_6_out;
  wire [0:0] and_3_out;
  wire [1:1] and_4_out;
  wire [2:2] and_1_out;

  not not_1 (not_1_out, Instruction[1]);
  not not_2 (not_2_out, Instruction[2]);
  not not_3 (not_3_out, Instruction[4]);
  and and_1 (and_1_out[2], Instruction[0], not_1_out, not_2_out, Instruction[3], not_3_out);
  not not_4 (not_4_out, State[1]);
  not not_5 (not_5_out, State[2]);
  not not_6 (not_6_out, State[0]);
  and and_2 (and_2_out, not_6_out, State[1], not_5_out);
  and and_3 (and_3_out[0], State[0], State[1], not_5_out);
  and and_4 (and_4_out[1], not_6_out, not_4_out, State[2]);
  and and_5 (RAM_Addr_Reg_Pass_through, and_1_out[2], and_2_out);
  assign RAM_Data_Reg_Sel = {2{and_1_out[2]}} & {and_4_out[1], 1'b0};  // AND_Gate and_6, 2 bits wide
  and and_7 (RAM_Write_Data, and_1_out[2], and_4_out[1]);
  and and_8 (RAM_Data_Reg_Pass_through, and_1_out[2], and_4_out[1]);
  and and_9 (ALU_I0_Reg_Enable, and_1_out[2], and_2_out);
  assign ALU_I1_Reg_Sel = {2{and_1_out[2]}} & {1'b0, and_3_out[0]};  // AND_Gate and_10, 2 bits wide
  and and_11 (ALU_Arith_Logic, and_1_out[2], and_4_out[1]);
  assign ALU_Mode = {3{and_1_out[2]}} & {2'b00, and_4_out[1]};  // AND_Gate and_12, 3 bits wide

  // Notes on the sheet:
  //   S2
  //   S3
  //   S4
endmodule

module CU_10_cmp__mem___mem (
  input  [4:0] Instruction,
  input  [2:0] State,
  output RAM_Addr_Reg_Pass_through,
  output ALU_I0_Reg_Enable,
  output [1:0] ALU_I1_Reg_Sel,
  output ALU_CMP
);

  wire and_2_out, and_4_out, and_5_out, and_6_out, not_1_out, not_2_out, not_3_out, not_4_out, not_5_out,
       not_6_out;
  wire [1:1] and_3_out;
  wire [2:2] and_1_out;

  not not_1 (not_1_out, Instruction[0]);
  not not_2 (not_2_out, Instruction[2]);
  not not_3 (not_3_out, Instruction[4]);
  and and_1 (and_1_out[2], not_1_out, Instruction[1], not_2_out, Instruction[3], not_3_out);
  not not_4 (not_4_out, State[1]);
  not not_5 (not_5_out, State[2]);
  not not_6 (not_6_out, State[0]);
  and and_2 (and_2_out, not_6_out, State[1], not_5_out);
  and and_3 (and_3_out[1], State[0], State[1], not_5_out);
  and and_4 (and_4_out, not_6_out, not_4_out, State[2]);
  and and_5 (and_5_out, and_1_out[2], and_2_out);
  and and_6 (and_6_out, and_1_out[2], and_3_out[1]);
  and and_7 (ALU_I0_Reg_Enable, and_1_out[2], and_2_out);
  assign ALU_I1_Reg_Sel = {2{and_1_out[2]}} & {and_3_out[1], 1'b0};  // AND_Gate and_8, 2 bits wide
  and and_9 (ALU_CMP, and_1_out[2], and_4_out);
  or or_1 (RAM_Addr_Reg_Pass_through, and_5_out, and_6_out);

  // Notes on the sheet:
  //   S2
  //   S3
  //   S4
endmodule

module CU_11_cmp__mem___con (
  input  [4:0] Instruction,
  input  [2:0] State,
  output RAM_Addr_Reg_Pass_through,
  output ALU_I0_Reg_Enable,
  output [1:0] ALU_I1_Reg_Sel,
  output ALU_CMP
);

  wire and_2_out, and_4_out, not_1_out, not_2_out, not_3_out, not_4_out, not_5_out;
  wire [0:0] and_3_out;
  wire [2:2] and_1_out;

  not not_1 (not_1_out, Instruction[2]);
  not not_2 (not_2_out, Instruction[4]);
  and and_1 (and_1_out[2], Instruction[0], Instruction[1], not_1_out, Instruction[3], not_2_out);
  not not_3 (not_3_out, State[1]);
  not not_4 (not_4_out, State[2]);
  not not_5 (not_5_out, State[0]);
  and and_2 (and_2_out, not_5_out, State[1], not_4_out);
  and and_3 (and_3_out[0], State[0], State[1], not_4_out);
  and and_4 (and_4_out, not_5_out, not_3_out, State[2]);
  and and_5 (RAM_Addr_Reg_Pass_through, and_1_out[2], and_2_out);
  and and_6 (ALU_I0_Reg_Enable, and_1_out[2], and_2_out);
  assign ALU_I1_Reg_Sel = {2{and_1_out[2]}} & {1'b0, and_3_out[0]};  // AND_Gate and_7, 2 bits wide
  and and_8 (ALU_CMP, and_1_out[2], and_4_out);

  // Notes on the sheet:
  //   S2
  //   S3
  //   S4
endmodule

module CU_12_mov__mem___mem (
  input  [4:0] Instruction,
  input  [2:0] State,
  output RAM_Addr_Reg_Pass_through,
  output [1:0] RAM_Data_Reg_Sel,
  output RAM_Write_Data,
  output RAM_Addr_Reg_Temp_Enable,
  output RAM_Addr_Reg_Temp_Use
);

  wire and_2_out, and_4_out, not_1_out, not_2_out, not_3_out, not_4_out, not_5_out, not_6_out;
  wire [1:1] and_3_out;
  wire [2:2] and_1_out;

  not not_1 (not_1_out, Instruction[0]);
  not not_2 (not_2_out, Instruction[1]);
  not not_3 (not_3_out, Instruction[4]);
  and and_1 (and_1_out[2], not_1_out, not_2_out, Instruction[2], Instruction[3], not_3_out);
  not not_4 (not_4_out, State[1]);
  not not_5 (not_5_out, State[2]);
  not not_6 (not_6_out, State[0]);
  and and_2 (and_2_out, not_6_out, State[1], not_5_out);
  and and_3 (and_3_out[1], State[0], State[1], not_5_out);
  and and_4 (and_4_out, not_6_out, not_4_out, State[2]);
  and and_5 (RAM_Addr_Reg_Pass_through, and_1_out[2], and_3_out[1]);
  assign RAM_Data_Reg_Sel = {2{and_1_out[2]}} & {2{and_3_out[1]}};  // AND_Gate and_6, 2 bits wide
  and and_7 (RAM_Write_Data, and_1_out[2], and_4_out);
  and and_8 (RAM_Addr_Reg_Temp_Enable, and_1_out[2], and_2_out);
  and and_9 (RAM_Addr_Reg_Temp_Use, and_1_out[2], and_4_out);

  // Notes on the sheet:
  //   S2
  //   S3
  //   S4
endmodule

module CU_13_mov__mem___con (
  input  [4:0] Instruction,
  input  [2:0] State,
  output RAM_Addr_Reg_Enable,
  output [1:0] RAM_Data_Reg_Sel,
  output RAM_Write_Data
);

  wire and_2_out, and_4_out, not_1_out, not_2_out, not_3_out, not_4_out, not_5_out;
  wire [0:0] and_3_out;
  wire [1:1] and_1_out;

  not not_1 (not_1_out, Instruction[1]);
  not not_2 (not_2_out, Instruction[4]);
  and and_1 (and_1_out[1], Instruction[0], not_1_out, Instruction[2], Instruction[3], not_2_out);
  not not_3 (not_3_out, State[0]);
  not not_4 (not_4_out, State[1]);
  not not_5 (not_5_out, State[2]);
  and and_2 (and_2_out, not_3_out, State[1], not_5_out);
  and and_3 (and_3_out[0], State[0], State[1], not_5_out);
  and and_4 (and_4_out, not_3_out, not_4_out, State[2]);
  and and_5 (RAM_Addr_Reg_Enable, and_1_out[1], and_2_out);
  assign RAM_Data_Reg_Sel = {2{and_1_out[1]}} & {1'b0, and_3_out[0]};  // AND_Gate and_6, 2 bits wide
  and and_7 (RAM_Write_Data, and_1_out[1], and_4_out);
endmodule

module CU_14_jmp__label (
  input  [4:0] Instruction,
  input  [2:0] State,
  output Enable_JMP,
  output JMP_Reg_Enable,
  output State_Input
);

  wire and_2_out, and_3_out, and_4_out, and_5_out, not_1_out, not_2_out, not_3_out, not_4_out, not_5_out;
  wire [2:2] and_1_out;

  not not_1 (not_1_out, Instruction[0]);
  not not_2 (not_2_out, Instruction[4]);
  and and_1 (and_1_out[2], not_1_out, Instruction[1], Instruction[2], Instruction[3], not_2_out);
  not not_3 (not_3_out, State[1]);
  not not_4 (not_4_out, State[2]);
  not not_5 (not_5_out, State[0]);
  and and_2 (and_2_out, not_5_out, State[1], not_4_out);
  and and_3 (and_3_out, State[0], State[1], not_4_out);
  and and_4 (and_4_out, not_5_out, not_3_out, State[2]);
  and and_5 (and_5_out, State[0], not_3_out, not_4_out);
  and and_6 (Enable_JMP, and_1_out[2], and_4_out);
  and and_7 (JMP_Reg_Enable, and_1_out[2], and_3_out);
  and and_8 (State_Input, and_1_out[2], and_5_out);

  // Notes on the sheet:
  //   State_Input: pull=down
  //   S2
  //   S3
  //   S4
  //   S1
endmodule

module CU_15_je__label (
  input  [4:0] Instruction,
  input  [2:0] State,
  output Cond_JMP_Enable,
  output [2:0] Cond_JMP_Mode,
  output JMP_Reg_Enable,
  output State_Input
);

  wire and_2_out, and_3_out, and_4_out, and_5_out, not_1_out, not_2_out, not_3_out, not_4_out;
  wire [2:2] and_1_out;

  not not_1 (not_1_out, Instruction[4]);
  and and_1 (and_1_out[2], Instruction[0], Instruction[1], Instruction[2], Instruction[3], not_1_out);
  not not_2 (not_2_out, State[1]);
  not not_3 (not_3_out, State[2]);
  not not_4 (not_4_out, State[0]);
  and and_2 (and_2_out, not_4_out, State[1], not_3_out);
  and and_3 (and_3_out, State[0], State[1], not_3_out);
  and and_4 (and_4_out, not_4_out, not_2_out, State[2]);
  and and_5 (and_5_out, State[0], not_2_out, not_3_out);
  and and_6 (Cond_JMP_Enable, and_1_out[2], and_4_out);
  assign Cond_JMP_Mode = {3{and_1_out[2]}} & 3'b000;  // AND_Gate and_7, 3 bits wide
  and and_8 (JMP_Reg_Enable, and_1_out[2], and_3_out);
  and and_9 (State_Input, and_1_out[2], and_5_out);

  // Notes on the sheet:
  //   State_Input: pull=down
  //   S2
  //   S3
  //   S4
  //   S1
endmodule

module CU_16_jne__label (
  input  [4:0] Instruction,
  input  [2:0] State,
  output Cond_JMP_Enable,
  output [2:0] Cond_JMP_Mode,
  output JMP_Reg_Enable,
  output State_Input
);

  wire and_2_out, and_3_out, and_5_out, not_1_out, not_2_out, not_3_out, not_4_out, not_5_out, not_6_out,
       not_7_out;
  wire [0:0] and_4_out;
  wire [2:2] and_1_out;

  not not_1 (not_1_out, Instruction[0]);
  not not_2 (not_2_out, Instruction[1]);
  not not_3 (not_3_out, Instruction[2]);
  not not_4 (not_4_out, Instruction[3]);
  and and_1 (and_1_out[2], not_1_out, not_2_out, not_3_out, not_4_out, Instruction[4]);
  not not_5 (not_5_out, State[1]);
  not not_6 (not_6_out, State[2]);
  not not_7 (not_7_out, State[0]);
  and and_2 (and_2_out, not_7_out, State[1], not_6_out);
  and and_3 (and_3_out, State[0], State[1], not_6_out);
  and and_4 (and_4_out[0], not_7_out, not_5_out, State[2]);
  and and_5 (and_5_out, State[0], not_5_out, not_6_out);
  and and_6 (Cond_JMP_Enable, and_1_out[2], and_4_out[0]);
  assign Cond_JMP_Mode = {3{and_1_out[2]}} & {2'b00, and_4_out[0]};  // AND_Gate and_7, 3 bits wide
  and and_8 (JMP_Reg_Enable, and_1_out[2], and_3_out);
  and and_9 (State_Input, and_1_out[2], and_5_out);

  // Notes on the sheet:
  //   State_Input: pull=down
  //   S2
  //   S3
  //   S4
  //   S1
endmodule

module CU_17_jg__label (
  input  [4:0] Instruction,
  input  [2:0] State,
  output Cond_JMP_Enable,
  output [2:0] Cond_JMP_Mode,
  output JMP_Reg_Enable,
  output State_Input
);

  wire and_2_out, and_3_out, and_5_out, not_1_out, not_2_out, not_3_out, not_4_out, not_5_out, not_6_out;
  wire [1:1] and_4_out;
  wire [2:2] and_1_out;

  not not_1 (not_1_out, Instruction[1]);
  not not_2 (not_2_out, Instruction[2]);
  not not_3 (not_3_out, Instruction[3]);
  and and_1 (and_1_out[2], Instruction[0], not_1_out, not_2_out, not_3_out, Instruction[4]);
  not not_4 (not_4_out, State[1]);
  not not_5 (not_5_out, State[2]);
  not not_6 (not_6_out, State[0]);
  and and_2 (and_2_out, not_6_out, State[1], not_5_out);
  and and_3 (and_3_out, State[0], State[1], not_5_out);
  and and_4 (and_4_out[1], not_6_out, not_4_out, State[2]);
  and and_5 (and_5_out, State[0], not_4_out, not_5_out);
  and and_6 (Cond_JMP_Enable, and_1_out[2], and_4_out[1]);
  assign Cond_JMP_Mode = {3{and_1_out[2]}} & {1'b0, and_4_out[1], 1'b0};  // AND_Gate and_7, 3 bits wide
  and and_8 (JMP_Reg_Enable, and_1_out[2], and_3_out);
  and and_9 (State_Input, and_1_out[2], and_5_out);

  // Notes on the sheet:
  //   State_Input: pull=down
  //   S2
  //   S3
  //   S4
  //   S1
endmodule

module CU_18_jge__label (
  input  [4:0] Instruction,
  input  [2:0] State,
  output Cond_JMP_Enable,
  output [2:0] Cond_JMP_Mode,
  output JMP_Reg_Enable,
  output State_Input
);

  wire and_2_out, and_3_out, and_5_out, not_1_out, not_2_out, not_3_out, not_4_out, not_5_out, not_6_out;
  wire [1:1] and_4_out;
  wire [2:2] and_1_out;

  not not_1 (not_1_out, Instruction[0]);
  not not_2 (not_2_out, Instruction[2]);
  not not_3 (not_3_out, Instruction[3]);
  and and_1 (and_1_out[2], not_1_out, Instruction[1], not_2_out, not_3_out, Instruction[4]);
  not not_4 (not_4_out, State[1]);
  not not_5 (not_5_out, State[2]);
  not not_6 (not_6_out, State[0]);
  and and_2 (and_2_out, not_6_out, State[1], not_5_out);
  and and_3 (and_3_out, State[0], State[1], not_5_out);
  and and_4 (and_4_out[1], not_6_out, not_4_out, State[2]);
  and and_5 (and_5_out, State[0], not_4_out, not_5_out);
  and and_6 (Cond_JMP_Enable, and_1_out[2], and_4_out[1]);
  assign Cond_JMP_Mode = {3{and_1_out[2]}} & {1'b0, {2{and_4_out[1]}}};  // AND_Gate and_7, 3 bits wide
  and and_8 (JMP_Reg_Enable, and_1_out[2], and_3_out);
  and and_9 (State_Input, and_1_out[2], and_5_out);

  // Notes on the sheet:
  //   State_Input: pull=down
  //   S2
  //   S3
  //   S4
  //   S1
endmodule

module CU_19_jl__label (
  input  [4:0] Instruction,
  input  [2:0] State,
  output Cond_JMP_Enable,
  output [2:0] Cond_JMP_Mode,
  output JMP_Reg_Enable,
  output State_Input
);

  wire and_2_out, and_3_out, and_5_out, not_1_out, not_2_out, not_3_out, not_4_out, not_5_out;
  wire [2:2] and_1_out, and_4_out;

  not not_1 (not_1_out, Instruction[2]);
  not not_2 (not_2_out, Instruction[3]);
  and and_1 (and_1_out[2], Instruction[0], Instruction[1], not_1_out, not_2_out, Instruction[4]);
  not not_3 (not_3_out, State[1]);
  not not_4 (not_4_out, State[2]);
  not not_5 (not_5_out, State[0]);
  and and_2 (and_2_out, not_5_out, State[1], not_4_out);
  and and_3 (and_3_out, State[0], State[1], not_4_out);
  and and_4 (and_4_out[2], not_5_out, not_3_out, State[2]);
  and and_5 (and_5_out, State[0], not_3_out, not_4_out);
  and and_6 (Cond_JMP_Enable, and_1_out[2], and_4_out[2]);
  assign Cond_JMP_Mode = {3{and_1_out[2]}} & {and_4_out[2], 2'b00};  // AND_Gate and_7, 3 bits wide
  and and_8 (JMP_Reg_Enable, and_1_out[2], and_3_out);
  and and_9 (State_Input, and_1_out[2], and_5_out);

  // Notes on the sheet:
  //   State_Input: pull=down
  //   S2
  //   S3
  //   S4
  //   S1
endmodule

module CU_20_jle__label (
  input  [4:0] Instruction,
  input  [2:0] State,
  output Cond_JMP_Enable,
  output [2:0] Cond_JMP_Mode,
  output JMP_Reg_Enable,
  output State_Input
);

  wire and_2_out, and_3_out, and_5_out, not_1_out, not_2_out, not_3_out, not_4_out, not_5_out, not_6_out;
  wire [2:2] and_1_out, and_4_out;

  not not_1 (not_1_out, Instruction[0]);
  not not_2 (not_2_out, Instruction[1]);
  not not_3 (not_3_out, Instruction[3]);
  and and_1 (and_1_out[2], not_1_out, not_2_out, Instruction[2], not_3_out, Instruction[4]);
  not not_4 (not_4_out, State[1]);
  not not_5 (not_5_out, State[2]);
  not not_6 (not_6_out, State[0]);
  and and_2 (and_2_out, not_6_out, State[1], not_5_out);
  and and_3 (and_3_out, State[0], State[1], not_5_out);
  and and_4 (and_4_out[2], not_6_out, not_4_out, State[2]);
  and and_5 (and_5_out, State[0], not_4_out, not_5_out);
  and and_6 (Cond_JMP_Enable, and_1_out[2], and_4_out[2]);
  assign Cond_JMP_Mode = {3{and_1_out[2]}} & {and_4_out[2], 1'b0, and_4_out[2]};  // AND_Gate and_7, 3 bits wide
  and and_8 (JMP_Reg_Enable, and_1_out[2], and_3_out);
  and and_9 (State_Input, and_1_out[2], and_5_out);

  // Notes on the sheet:
  //   State_Input: pull=down
  //   S2
  //   S3
  //   S4
  //   S1
endmodule

module CU_21_jz__label (
  input  [4:0] Instruction,
  input  [2:0] State,
  output Cond_JMP_Enable,
  output [2:0] Cond_JMP_Mode,
  output JMP_Reg_Enable,
  output State_Input
);

  wire and_2_out, and_3_out, and_5_out, not_1_out, not_2_out, not_3_out, not_4_out, not_5_out;
  wire [2:2] and_1_out, and_4_out;

  not not_1 (not_1_out, Instruction[1]);
  not not_2 (not_2_out, Instruction[3]);
  and and_1 (and_1_out[2], Instruction[0], not_1_out, Instruction[2], not_2_out, Instruction[4]);
  not not_3 (not_3_out, State[1]);
  not not_4 (not_4_out, State[2]);
  not not_5 (not_5_out, State[0]);
  and and_2 (and_2_out, not_5_out, State[1], not_4_out);
  and and_3 (and_3_out, State[0], State[1], not_4_out);
  and and_4 (and_4_out[2], not_5_out, not_3_out, State[2]);
  and and_5 (and_5_out, State[0], not_3_out, not_4_out);
  and and_6 (Cond_JMP_Enable, and_1_out[2], and_4_out[2]);
  assign Cond_JMP_Mode = {3{and_1_out[2]}} & {{2{and_4_out[2]}}, 1'b0};  // AND_Gate and_7, 3 bits wide
  and and_8 (JMP_Reg_Enable, and_1_out[2], and_3_out);
  and and_9 (State_Input, and_1_out[2], and_5_out);

  // Notes on the sheet:
  //   State_Input: pull=down
  //   S2
  //   S3
  //   S4
  //   S1
endmodule

module CU_22_jnz__label (
  input  [4:0] Instruction,
  input  [2:0] State,
  output Cond_JMP_Enable,
  output [2:0] Cond_JMP_Mode,
  output JMP_Reg_Enable,
  output State_Input
);

  wire and_2_out, and_3_out, and_5_out, not_1_out, not_2_out, not_3_out, not_4_out, not_5_out;
  wire [2:2] and_1_out, and_4_out;

  not not_1 (not_1_out, Instruction[0]);
  not not_2 (not_2_out, Instruction[3]);
  and and_1 (and_1_out[2], not_1_out, Instruction[1], Instruction[2], not_2_out, Instruction[4]);
  not not_3 (not_3_out, State[1]);
  not not_4 (not_4_out, State[2]);
  not not_5 (not_5_out, State[0]);
  and and_2 (and_2_out, not_5_out, State[1], not_4_out);
  and and_3 (and_3_out, State[0], State[1], not_4_out);
  and and_4 (and_4_out[2], not_5_out, not_3_out, State[2]);
  and and_5 (and_5_out, State[0], not_3_out, not_4_out);
  and and_6 (Cond_JMP_Enable, and_1_out[2], and_4_out[2]);
  assign Cond_JMP_Mode = {3{and_1_out[2]}} & {3{and_4_out[2]}};  // AND_Gate and_7, 3 bits wide
  and and_8 (JMP_Reg_Enable, and_1_out[2], and_3_out);
  and and_9 (State_Input, and_1_out[2], and_5_out);

  // Notes on the sheet:
  //   State_Input: pull=down
  //   S2
  //   S3
  //   S4
  //   S1
endmodule

module CU_23_inc__mem (
  input  [4:0] Instruction,
  input  [2:0] State,
  output RAM_Addr_Reg_Pass_through,
  output [1:0] RAM_Data_Reg_Sel,
  output RAM_Write_Data,
  output RAM_Data_Reg_Pass_through,
  output State_Input,
  output ALU_I0_Reg_Enable,
  output ALU_Arith_Logic,
  output [2:0] ALU_Mode
);

  wire and_2_out, and_3_out, and_5_out, not_1_out, not_2_out, not_3_out, not_4_out;
  wire [1:1] and_4_out;
  wire [2:2] and_1_out;

  not not_1 (not_1_out, Instruction[3]);
  and and_1 (and_1_out[2], Instruction[0], Instruction[1], Instruction[2], not_1_out, Instruction[4]);
  not not_2 (not_2_out, State[1]);
  not not_3 (not_3_out, State[2]);
  not not_4 (not_4_out, State[0]);
  and and_2 (and_2_out, not_4_out, State[1], not_3_out);
  and and_3 (and_3_out, State[0], State[1], not_3_out);
  and and_4 (and_4_out[1], not_4_out, not_2_out, State[2]);
  and and_5 (and_5_out, State[0], not_2_out, not_3_out);
  and and_6 (RAM_Addr_Reg_Pass_through, and_1_out[2], and_3_out);
  assign RAM_Data_Reg_Sel = {2{and_1_out[2]}} & {and_4_out[1], 1'b0};  // AND_Gate and_7, 2 bits wide
  and and_8 (RAM_Write_Data, and_1_out[2], and_4_out[1]);
  and and_9 (RAM_Data_Reg_Pass_through, and_1_out[2], and_4_out[1]);
  and and_10 (State_Input, and_1_out[2], and_5_out);
  and and_11 (ALU_I0_Reg_Enable, and_1_out[2], and_3_out);
  and and_12 (ALU_Arith_Logic, and_1_out[2], and_4_out[1]);
  assign ALU_Mode = {3{and_1_out[2]}} & {1'b0, and_4_out[1], 1'b0};  // AND_Gate and_13, 3 bits wide

  // Notes on the sheet:
  //   State_Input: pull=down
  //   S2
  //   S3
  //   S4
  //   S1
endmodule

module CU_24_dec__mem (
  input  [4:0] Instruction,
  input  [2:0] State,
  output RAM_Addr_Reg_Pass_through,
  output [1:0] RAM_Data_Reg_Sel,
  output RAM_Write_Data,
  output RAM_Data_Reg_Pass_through,
  output State_Input,
  output ALU_I0_Reg_Enable,
  output ALU_Arith_Logic,
  output [2:0] ALU_Mode
);

  wire and_2_out, and_3_out, and_5_out, not_1_out, not_2_out, not_3_out, not_4_out, not_5_out, not_6_out;
  wire [1:1] and_4_out;
  wire [2:2] and_1_out;

  not not_1 (not_1_out, Instruction[0]);
  not not_2 (not_2_out, Instruction[1]);
  not not_3 (not_3_out, Instruction[2]);
  and and_1 (and_1_out[2], not_1_out, not_2_out, not_3_out, Instruction[3], Instruction[4]);
  not not_4 (not_4_out, State[1]);
  not not_5 (not_5_out, State[2]);
  not not_6 (not_6_out, State[0]);
  and and_2 (and_2_out, not_6_out, State[1], not_5_out);
  and and_3 (and_3_out, State[0], State[1], not_5_out);
  and and_4 (and_4_out[1], not_6_out, not_4_out, State[2]);
  and and_5 (and_5_out, State[0], not_4_out, not_5_out);
  and and_6 (RAM_Addr_Reg_Pass_through, and_1_out[2], and_3_out);
  assign RAM_Data_Reg_Sel = {2{and_1_out[2]}} & {and_4_out[1], 1'b0};  // AND_Gate and_7, 2 bits wide
  and and_8 (RAM_Write_Data, and_1_out[2], and_4_out[1]);
  and and_9 (RAM_Data_Reg_Pass_through, and_1_out[2], and_4_out[1]);
  and and_10 (State_Input, and_1_out[2], and_5_out);
  and and_11 (ALU_I0_Reg_Enable, and_1_out[2], and_3_out);
  and and_12 (ALU_Arith_Logic, and_1_out[2], and_4_out[1]);
  assign ALU_Mode = {3{and_1_out[2]}} & {1'b0, {2{and_4_out[1]}}};  // AND_Gate and_13, 3 bits wide

  // Notes on the sheet:
  //   State_Input: pull=down
  //   S2
  //   S3
  //   S4
  //   S1
endmodule

module CU_25_xor__mem___mem (
  input  [4:0] Instruction,
  input  [2:0] State,
  output RAM_Addr_Reg_Pass_through,
  output RAM_Data_Reg_Pass_through,
  output [1:0] RAM_Data_Reg_Sel,
  output RAM_Write_Data,
  output RAM_Addr_Reg_Temp_Enable,
  output RAM_Addr_Reg_Temp_Use,
  output ALU_I0_Reg_Enable,
  output [1:0] ALU_I1_Reg_Sel,
  output [2:0] ALU_Mode
);

  wire and_2_out, and_5_out, and_6_out, not_1_out, not_2_out, not_3_out, not_4_out, not_5_out;
  wire [1:1] and_3_out, and_4_out;
  wire [2:2] and_1_out;

  not not_1 (not_1_out, Instruction[1]);
  not not_2 (not_2_out, Instruction[2]);
  and and_1 (and_1_out[2], Instruction[0], not_1_out, not_2_out, Instruction[3], Instruction[4]);
  not not_3 (not_3_out, State[1]);
  not not_4 (not_4_out, State[2]);
  not not_5 (not_5_out, State[0]);
  and and_2 (and_2_out, not_5_out, State[1], not_4_out);
  and and_3 (and_3_out[1], State[0], State[1], not_4_out);
  and and_4 (and_4_out[1], not_5_out, not_3_out, State[2]);
  and and_5 (and_5_out, and_1_out[2], and_2_out);
  and and_6 (and_6_out, and_1_out[2], and_3_out[1]);
  or or_1 (RAM_Addr_Reg_Pass_through, and_5_out, and_6_out);
  and and_7 (RAM_Data_Reg_Pass_through, and_1_out[2], and_4_out[1]);
  assign RAM_Data_Reg_Sel = {2{and_1_out[2]}} & {and_4_out[1], 1'b0};  // AND_Gate and_8, 2 bits wide
  and and_9 (RAM_Write_Data, and_1_out[2], and_4_out[1]);
  and and_10 (RAM_Addr_Reg_Temp_Enable, and_1_out[2], and_2_out);
  and and_11 (RAM_Addr_Reg_Temp_Use, and_1_out[2], and_4_out[1]);
  and and_12 (ALU_I0_Reg_Enable, and_1_out[2], and_2_out);
  assign ALU_I1_Reg_Sel = {2{and_1_out[2]}} & {and_3_out[1], 1'b0};  // AND_Gate and_13, 2 bits wide
  assign ALU_Mode = {3{and_1_out[2]}} & {1'b0, {2{and_4_out[1]}}};  // AND_Gate and_14, 3 bits wide

  // Notes on the sheet:
  //   S2
  //   S3
  //   S4
endmodule

module CU_26_xor__mem___con (
  input  [4:0] Instruction,
  input  [2:0] State,
  output RAM_Addr_Reg_Pass_through,
  output RAM_Data_Reg_Pass_through,
  output [1:0] RAM_Data_Reg_Sel,
  output RAM_Write_Data,
  output ALU_I0_Reg_Enable,
  output [1:0] ALU_I1_Reg_Sel,
  output [2:0] ALU_Mode
);

  wire and_2_out, not_1_out, not_2_out, not_3_out, not_4_out, not_5_out;
  wire [0:0] and_3_out;
  wire [1:1] and_4_out;
  wire [2:2] and_1_out;

  not not_1 (not_1_out, Instruction[0]);
  not not_2 (not_2_out, Instruction[2]);
  and and_1 (and_1_out[2], not_1_out, Instruction[1], not_2_out, Instruction[3], Instruction[4]);
  not not_3 (not_3_out, State[1]);
  not not_4 (not_4_out, State[2]);
  not not_5 (not_5_out, State[0]);
  and and_2 (and_2_out, not_5_out, State[1], not_4_out);
  and and_3 (and_3_out[0], State[0], State[1], not_4_out);
  and and_4 (and_4_out[1], not_5_out, not_3_out, State[2]);
  and and_5 (RAM_Addr_Reg_Pass_through, and_1_out[2], and_2_out);
  and and_6 (RAM_Data_Reg_Pass_through, and_1_out[2], and_4_out[1]);
  assign RAM_Data_Reg_Sel = {2{and_1_out[2]}} & {and_4_out[1], 1'b0};  // AND_Gate and_7, 2 bits wide
  and and_8 (RAM_Write_Data, and_1_out[2], and_4_out[1]);
  and and_9 (ALU_I0_Reg_Enable, and_1_out[2], and_2_out);
  assign ALU_I1_Reg_Sel = {2{and_1_out[2]}} & {1'b0, and_3_out[0]};  // AND_Gate and_10, 2 bits wide
  assign ALU_Mode = {3{and_1_out[2]}} & {1'b0, {2{and_4_out[1]}}};  // AND_Gate and_11, 3 bits wide

  // Notes on the sheet:
  //   S2
  //   S3
  //   S4
endmodule

module CU_27_out__mem (
  input  [4:0] Instruction,
  input  [2:0] State,
  output RAM_Addr_Reg_Pass_through,
  output State_Input,
  output Output_Reg_Enable
);

  wire and_2_out, and_3_out, and_4_out, and_5_out, not_1_out, not_2_out, not_3_out, not_4_out;
  wire [2:2] and_1_out;

  not not_1 (not_1_out, Instruction[2]);
  and and_1 (and_1_out[2], Instruction[0], Instruction[1], not_1_out, Instruction[3], Instruction[4]);
  not not_2 (not_2_out, State[1]);
  not not_3 (not_3_out, State[2]);
  not not_4 (not_4_out, State[0]);
  and and_2 (and_2_out, not_4_out, State[1], not_3_out);
  and and_3 (and_3_out, State[0], State[1], not_3_out);
  and and_4 (and_4_out, not_4_out, not_2_out, State[2]);
  and and_5 (and_5_out, State[0], not_2_out, not_3_out);
  and and_6 (RAM_Addr_Reg_Pass_through, and_1_out[2], and_3_out);
  and and_7 (State_Input, and_1_out[2], and_5_out);
  and and_8 (Output_Reg_Enable, and_1_out[2], and_4_out);

  // Notes on the sheet:
  //   State_Input: pull=down
  //   S2
  //   S3
  //   S4
  //   S1
endmodule

module CU_FSM (
  input  Input,
  output [2:0] State
);

  wire and_1_out, and_2_out, and_3_out, and_4_out, and_5_out, Clk_out, d_ff_1_qn, d_ff_2_qn, d_ff_3_qn,
       not_1_out, or_1_out, or_2_out;

  Clock Clk (.out(Clk_out));
  not not_1 (not_1_out, Input);
  and and_1 (and_1_out, not_1_out, d_ff_3_qn, d_ff_1_qn);
  and and_2 (and_2_out, Input, d_ff_3_qn, d_ff_2_qn, State[0]);
  and and_3 (and_3_out, d_ff_3_qn, d_ff_2_qn, State[0]);
  and and_4 (and_4_out, not_1_out, d_ff_3_qn, State[1], d_ff_1_qn);
  and and_5 (and_5_out, not_1_out, d_ff_3_qn, State[1], State[0]);
  or or_1 (or_1_out, and_1_out, and_2_out);
  or or_2 (or_2_out, and_3_out, and_4_out);
  D_Flip_Flop d_ff_1 (.clk(Clk_out), .D(or_1_out), .Q(State[0]), .Qn(d_ff_1_qn));  // open: preset, en, reset
  D_Flip_Flop d_ff_2 (.clk(Clk_out), .D(or_2_out), .Q(State[1]), .Qn(d_ff_2_qn));  // open: preset, en, reset
  D_Flip_Flop d_ff_3 (.clk(Clk_out), .D(and_5_out), .Q(State[2]), .Qn(d_ff_3_qn));  // open: preset, en, reset

  // Notes on the sheet:
  //   Q2
  //   I
  //   Q1
  //   Q0
  //   Q0+
  //   Q1+
  //   Q2+
  //   Q0
  //   Q1
  //   Q2
endmodule
